// Logisim project f_2407.circ as structural Verilog: 8 circuits, main circuit minirv_soc
module minirv_soc (
  input  rst_i
);

  wire clk_i, comparator_1_eq, comparator_1_gt, comparator_2_lt, isMem, isVGA, mem_wr_en, or_1_out;
  wire [3:0] mem_wr_mask;
  wire [17:0] pc;
  wire [31:0] inst, mem_addr, mem_rd_data, mem_wr_data, minirv_core_1_pc_o, minirv_core_1_perf_o;

  Clock u_clk_i (.out(clk_i));
  ROM #(.addrWidth(18), .dataWidth(32)) rom_1 (.addr(pc), .data(inst));
  RAM #(.addrWidth(18), .asyncread("true"), .byteenables("byteEnables"), .dataWidth(32), .\type ("nonvolatile")) ram_1 (
    .addr(mem_addr[19:2]), .we(isMem), .oe(1'b1), .clk(clk_i), .din(mem_wr_data), .dout(mem_rd_data),
    .be3(mem_wr_mask[3]), .be2(mem_wr_mask[2]), .be1(mem_wr_mask[1]), .be0(mem_wr_mask[0]));
  // Probe on mem_wr_data
  minirv_core minirv_core_1 (
    .clk_i(clk_i), .rst_i(rst_i), .inst_i(inst), .mem_rd_data_i(mem_rd_data),
    .pc_o({minirv_core_1_pc_o[31:20], pc, minirv_core_1_pc_o[1:0]}), .mem_addr_o(mem_addr),
    .mem_wr_en_o(mem_wr_en), .mem_wr_mask_o(mem_wr_mask), .mem_wr_data_o(mem_wr_data),
    .perf_o(minirv_core_1_perf_o));
  // Probe on minirv_core_1_perf_o
  // RGB_Video #(.cursor("No Cursor"), .height(256), .width(256)) rgb_video_1: pin names not known; wires that end beside it: rst_i, clk_i, isVGA, mem_addr[9:2], mem_addr[17:10], mem_wr_data[23:0]
  Comparator #(.mode("unsigned"), .width(32)) comparator_1 (
    .a(mem_addr), .b(32'h20000000), .gt(comparator_1_gt), .eq(comparator_1_eq));  // open: lt
  Comparator #(.mode("unsigned"), .width(32)) comparator_2 (
    .a(mem_addr), .b(32'h20040000), .lt(comparator_2_lt));  // open: gt, eq
  or or_1 (or_1_out, comparator_1_gt, comparator_1_eq);
  not not_1 (isMem, isVGA);
  and and_1 (isVGA, or_1_out, comparator_2_lt, mem_wr_en);

  // Notes on the sheet:
  //   contents of rom_1 (hex, n*v repeats v):
  //   413 93137 10113 10b7 dbc08093 80e7 fe012823 fea10923 fea12423 fe914203 fe4109a3 ff012783 f787b3
  //   f787b3 4b6b7 f0068693 fdc10113 d787b3 10000713 f12423 10593 100793 b00513 2112023 12023 12223 e12623
  //   e12823 f10a23 10b7 a8408093 80e7 2012083 2410113 8067 ff410113 112423 10b7 a7c08093 80e7 513 1800093
  //   80e7 812083 513 c10113 8067 852583 feb12823 fe812e23 3437 a0840413 ff014183 3401b3 1c183 ff114203
  //   440233 24203 4181b3 ff214203 440233 24203 4181b3 ff314203 440233 24203 4181b3 3237 a0020213 320233
  //   24203 ffc12403 420233 420233 410233 11b7 85c18193 fe312823 14800193 fe312623 fec22203 20067 1052703
  //   52683 452783 fe810113 e12423 112a23 fed12823 fef12623 13737 c0070713 fe012223 ff314203 fe4102a3
  //   fef14203 fe410223 fe412203 470233 24203 fe4105a3 ff214203 fe4102a3 fee14203 fe410223 fe412203 470233
  //   24203 fe410523 ff114203 fe4102a3 fed14203 fe410223 fe412203 470233 24203 fe4104a3 ff014203 fe4102a3
  //   fec14203 fe410223 fe412203 470233 24203 fe410423 fe812703 c52603 fee12823 fe812e23 3437 a0840413
  //   ff014183 3401b3 1c183 ff114203 440233 24203 4181b3 ff214203 440233 24203 4181b3 ff314203 440233
  //   24203 4181b3 3237 a0020213 320233 24203 ffc12403 420233 420233 410233 66800193 fe312823 28000193
  //   fe312623 fec22203 20067 c68733 10000513 fe812e23 fe912c23 fee12823 50413 ff012483 fe812423 feb14183
  //   3181b3 fe312423 fe914183 3181b3 fe912423 feb14203 420233 fe412423 fe914203 4181b3 3181b3 fe312a23
  //   fe912423 33237 b0020213 feb14183 4181b3 1c183 fe3103a3 fea14183 4181b3 1c183 fe310323 fe914183
  //   4181b3 1c183 fe3102a3 fe814183 4181b3 1c183 fe310223 ff412183 fe412203 440233 120213 fe412423
  //   feb14203 420233 fe412423 fe914203 4181b3 3237 b0820213 320233 ff812483 ffc12403 24203 420233 420233
  //   410233 11b7 86018193 fe312823 38800193 fe312623 fec22203 20067 812703 10000513 812823 e78733
  //   fe812e23 fe912c23 fee12823 50413 ff012483 fe812423 feb14183 3181b3 fe312423 fe914183 3181b3 fe912423
  //   feb14203 420233 fe412423 fe914203 4181b3 3181b3 fe312a23 fe912423 33237 b0020213 feb14183 4181b3
  //   1c183 fe3103a3 fea14183 4181b3 1c183 fe310323 fe914183 4181b3 1c183 fe3102a3 fe814183 4181b3 1c183
  //   fe310223 ff412183 fe412203 440233 120213 fe412423 feb14203 420233 fe412423 fe914203 4181b3 3237
  //   b0820213 320233 ff812483 ffc12403 24203 420233 420233 410233 11b7 86418193 fe312823 49800193
  //   fe312623 fec22203 20067 8*f787b3 d787b3 f787b3 f787b3 20000437 f40433 812783 c60633 c60633 fef12423
  //   feb14183 3181b3 fe312423 fe914183 fff78213 fe412423 feb14203 420233 fe412423 fe914203 4181b3 3237
  //   b1820213 418233 24203 420233 420233 410233 65800193 fe312823 53c00193 fe312623 fec22203 20067 912623
  //   493 40513 c12223 b12023 10b7 de008093 80e7 12583 412603 812783 148493 40040413 c585b3 fef12823
  //   fe912623 fe812e23 fe912c23 4b437 d0040413 ff014183 340233 100193 320023 fec14183 3401b3 18023 24183
  //   ff114483 940233 100493 920023 fed14483 9404b3 48023 24483 9181b3 ff214483 940233 100493 920023
  //   fee14483 9404b3 48023 24483 9181b3 ff314483 940233 100493 920023 fef14483 9404b3 48023 24483 9181b3
  //   3237 a0020213 320233 24203 ff812483 ffc12403 420233 420233 410233 65400193 fe312823 54400193
  //   fe312623 fec22203 20067 c12483 1012403 1412083 1810113 8067 10000713 fec12823 fee12623 fe812e23
  //   fe912c23 4b437 d0040413 ff014183 340233 100193 320023 fec14183 3401b3 18023 24183 ff114483 940233
  //   100493 920023 fed14483 9404b3 48023 24483 9181b3 ff214483 940233 100493 920023 fee14483 9404b3 48023
  //   24483 9181b3 ff314483 940233 100493 920023 fef14483 9404b3 48023 24483 9181b3 3237 a0020213 320233
  //   24203 ff812483 ffc12403 420233 420233 410233 74c00193 fe312823 28000193 fe312623 fec22203 20067
  //   812703 fee12823 fec12623 fe812e23 fe912c23 4b437 d0040413 ff014183 340233 100193 320023 fec14183
  //   3401b3 18023 24183 ff114483 940233 100493 920023 fed14483 9404b3 48023 24483 9181b3 ff214483 940233
  //   100493 920023 fee14483 9404b3 48023 24483 9181b3 ff314483 940233 100493 920023 fef14483 9404b3 48023
  //   24483 9181b3 3237 a0020213 320233 24203 ff812483 ffc12403 420233 420233 410233 11b7 83418193
  //   fe312823 38800193 fe312623 fec22203 20067 1412083 40637 20000537 1810113 1237 de020213 20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
  //   Copyright (c) 2026 Guiyuan Zhu. All rights reserved.
endmodule

module minirv_core (
  input  clk_i,
  input  rst_i,
  input  [31:0] inst_i,
  input  [31:0] mem_rd_data_i,
  output [31:0] pc_o,
  output [31:0] mem_addr_o,
  output mem_wr_en_o,
  output [3:0] mem_wr_mask_o,
  output [31:0] mem_wr_data_o,
  output [31:0] perf_o
);

  wire is_add, is_addi, is_jalr, is_lbu, is_lui, is_lw, ls_sb, ls_sw, rd_wr_en;
  wire [4:0] rd, rs1, rs2;
  wire [31:0] alu_result, imm, mem_rd_data, pc_nxt, rd_val, rs1_val, rs2_val;

  // Probe on inst_i
  minirv_decoder minirv_decoder_1 (
    .inst_i(inst_i), .is_add_o(is_add), .is_addi_o(is_addi), .is_lui_o(is_lui), .is_lw_o(is_lw),
    .is_lbu_o(is_lbu), .is_sw_o(ls_sw), .is_sb_o(ls_sb), .is_jalr_o(is_jalr), .imm_o(imm), .rs1_o(rs1),
    .rs2_o(rs2), .rd_o(rd));
  // Probe on pc_o
  minirv_pc minirv_pc_1 (
    .clk_i(clk_i), .rst_i(rst_i), .load_en_i(is_jalr), .load_data_i(alu_result), .pc_o(pc_o),
    .pc_nxt_o(pc_nxt), .perf_o(perf_o));
  // Probe on rd
  minirv_alu minirv_alu_1 (
    .imm_i(imm), .data0_i(rs1_val), .data1_i(rs2_val), .is_add_i(is_add), .is_addi_i(is_addi),
    .is_lui_i(is_lui), .is_lw_i(is_lw), .is_lbu_i(is_lbu), .is_sw_i(ls_sw), .is_sb_i(ls_sb),
    .is_jalr_i(is_jalr), .data_o(alu_result));
  // Probe on alu_result
  // Probe on rd_val
  minirv_gpr_rd_driver minirv_gpr_rd_driver_1 (
    .alu_result_i(alu_result), .pc_nxt_i(pc_nxt), .mem_data_i(mem_rd_data), .is_add_i(is_add),
    .is_addi_i(is_addi), .is_lui_i(is_lui), .is_lw_i(is_lw), .is_lbu_i(is_lbu), .is_sw_i(ls_sw),
    .is_sb_i(ls_sb), .is_jalr_i(is_jalr), .rd_val_o(rd_val), .rd_wr_en_o(rd_wr_en));
  minirv_gpr minirv_gpr_1 (
    .clk_i(clk_i), .wr_data_i(rd_val), .wr_addr_i(rd), .wr_en_i(rd_wr_en), .rd_addr0_i(rs1),
    .rd_addr1_i(rs2), .rd_data0_o(rs1_val), .rd_data1_o(rs2_val));
  minirv_mem_driver minirv_mem_driver_1 (
    .alu_result_i(alu_result), .rs2_val_i(rs2_val), .is_lw_i(is_lw), .is_lbu_i(is_lbu), .is_sw_i(ls_sw),
    .is_sb_i(ls_sb), .mem_rd_data_i(mem_rd_data_i), .mem_addr_o(mem_addr_o), .mem_wr_en_o(mem_wr_en_o),
    .mem_wr_mask_o(mem_wr_mask_o), .mem_wr_data_o(mem_wr_data_o), .mem_rd_data_o(mem_rd_data));

  // Other names for the same wires on the sheet: inst[31:0] = inst_i; mem_addr[31:0] = mem_addr_o;
  //   mem_rd_data_raw[31:0] = mem_rd_data_i; mem_wr_data[31:0] = mem_wr_data_o; mem_wr_en = mem_wr_en_o;
  //   mem_wr_mask[3:0] = mem_wr_mask_o; pc[31:0] = pc_o; perf[31:0] = perf_o

  // Notes on the sheet:
  //   Copyright (c) 2026 Guiyuan Zhu. All rights reserved.
endmodule

module minirv_decoder (
  input  [31:0] inst_i,
  output is_add_o,
  output is_addi_o,
  output is_lui_o,
  output is_lw_o,
  output is_lbu_o,
  output is_sw_o,
  output is_sb_o,
  output is_jalr_o,
  output [31:0] imm_o,
  output [4:0] rs1_o,
  output [4:0] rs2_o,
  output [4:0] rd_o
);

  wire comparator_1_eq, comparator_2_eq, comparator_3_eq, comparator_4_eq, comparator_5_eq, comparator_7_eq,
       comparator_8_eq, comparator_9_eq, comparator_10_eq, comparator_11_eq, comparator_12_eq,
       comparator_13_eq, comparator_14_eq, comparator_15_eq, comparator_16_eq, or_1_out, or_2_out;
  wire [31:0] and_8_out, and_9_out, and_10_out, bit_extender_3_out, bit_extender_4_out, bit_extender_5_out;
  wire [31:11] i_imm, s_imm;

  assign i_imm = {{20{inst_i[31]}}, inst_i[31]};  // Bit_Extender bit_extender_1
  assign s_imm = {{20{inst_i[31]}}, inst_i[31]};  // Bit_Extender bit_extender_2
  Comparator #(.width(7)) comparator_1 (.a(7'b0110011), .b(inst_i[6:0]), .eq(comparator_1_eq));  // open: gt, lt
  and and_1 (is_add_o, comparator_1_eq, comparator_2_eq, comparator_3_eq);
  Comparator #(.width(3)) comparator_2 (.a(3'b000), .b(inst_i[14:12]), .eq(comparator_2_eq));  // open: gt, lt
  Comparator #(.width(7)) comparator_3 (.a({7{1'b0}}), .b(inst_i[31:25]), .eq(comparator_3_eq));  // open: gt, lt
  Comparator #(.width(7)) comparator_4 (.a(7'b0010011), .b(inst_i[6:0]), .eq(comparator_4_eq));  // open: gt, lt
  and and_2 (is_addi_o, comparator_4_eq, comparator_5_eq);
  Comparator #(.width(3)) comparator_5 (.a(3'b000), .b(inst_i[14:12]), .eq(comparator_5_eq));  // open: gt, lt
  Comparator #(.width(7)) comparator_6 (.a(7'b0110111), .b(inst_i[6:0]), .eq(is_lui_o));  // open: gt, lt
  Comparator #(.width(7)) comparator_7 (.a(7'b0000011), .b(inst_i[6:0]), .eq(comparator_7_eq));  // open: gt, lt
  Comparator #(.width(3)) comparator_8 (.a(3'b010), .b(inst_i[14:12]), .eq(comparator_8_eq));  // open: gt, lt
  Comparator #(.width(7)) comparator_9 (.a(7'b0000011), .b(inst_i[6:0]), .eq(comparator_9_eq));  // open: gt, lt
  Comparator #(.width(3)) comparator_10 (.a(3'b100), .b(inst_i[14:12]), .eq(comparator_10_eq));  // open: gt, lt
  Comparator #(.width(7)) comparator_11 (.a(7'b0100011), .b(inst_i[6:0]), .eq(comparator_11_eq));  // open: gt, lt
  Comparator #(.width(3)) comparator_12 (.a(3'b010), .b(inst_i[14:12]), .eq(comparator_12_eq));  // open: gt, lt
  Comparator #(.width(7)) comparator_13 (.a(7'b0100011), .b(inst_i[6:0]), .eq(comparator_13_eq));  // open: gt, lt
  Comparator #(.width(3)) comparator_14 (.a(3'b000), .b(inst_i[14:12]), .eq(comparator_14_eq));  // open: gt, lt
  Comparator #(.width(7)) comparator_15 (.a(7'b1100111), .b(inst_i[6:0]), .eq(comparator_15_eq));  // open: gt, lt
  Comparator #(.width(3)) comparator_16 (.a(3'b000), .b(inst_i[14:12]), .eq(comparator_16_eq));  // open: gt, lt
  assign bit_extender_3_out = {{31{or_1_out}}, or_1_out};  // Bit_Extender bit_extender_3
  or or_1 (or_1_out, is_addi_o, is_lw_o, is_lbu_o, is_jalr_o);
  assign bit_extender_4_out = {{31{or_2_out}}, or_2_out};  // Bit_Extender bit_extender_4
  or or_2 (or_2_out, is_sw_o, is_sb_o);
  assign bit_extender_5_out = {{31{is_lui_o}}, is_lui_o};  // Bit_Extender bit_extender_5
  and and_3 (is_lw_o, comparator_7_eq, comparator_8_eq);
  and and_4 (is_lbu_o, comparator_9_eq, comparator_10_eq);
  and and_5 (is_sw_o, comparator_11_eq, comparator_12_eq);
  and and_6 (is_sb_o, comparator_13_eq, comparator_14_eq);
  and and_7 (is_jalr_o, comparator_15_eq, comparator_16_eq);
  assign and_8_out = {i_imm, inst_i[30:20]} & bit_extender_3_out;  // AND_Gate and_8, 32 bits wide
  assign and_9_out = {s_imm, inst_i[30:25], inst_i[11:7]} & bit_extender_4_out;  // AND_Gate and_9, 32 bits wide
  assign and_10_out = {inst_i[31:12], {12{1'b0}}} & bit_extender_5_out;  // AND_Gate and_10, 32 bits wide
  assign imm_o = and_8_out | and_9_out | and_10_out;  // OR_Gate or_3, 32 bits wide

  assign rd_o = inst_i[11:7];
  assign rs1_o = inst_i[19:15];
  assign rs2_o = inst_i[24:20];

  // Other names for the same wires on the sheet: imm[31:0] = imm_o; inst[31:0] = inst_i; opcode[6:0] = inst_i[6:0];
  //   is_add = is_add_o; is_addi = is_addi_o; is_jalr = is_jalr_o; is_lbu = is_lbu_o; is_lui = is_lui_o;
  //   is_lw = is_lw_o; is_sb = is_sb_o; is_sw = is_sw_o; inst_7 = inst_i[7]; rd[4:0] = inst_i[11:7];
  //   s_imm[10:0] = {inst_i[30:25], inst_i[11:7]}; inst_11_8[3:0] = inst_i[11:8]; funct3[2:0] = inst_i[14:12];
  //   inst_19_12[7:0] = inst_i[19:12]; u_imm[31:12] = inst_i[31:12]; rs1[4:0] = inst_i[19:15];
  //   i_imm[10:0] = inst_i[30:20]; inst_20 = inst_i[20]; inst_30_20[10:0] = inst_i[30:20]; rs2[4:0] = inst_i[24:20];
  //   inst_24_21[3:0] = inst_i[24:21]; funct7[6:0] = inst_i[31:25]; inst_30_25[5:0] = inst_i[30:25];
  //   inst_31 = inst_i[31]

  // Notes on the sheet:
  //   Copyright (c) 2026 Guiyuan Zhu. All rights reserved.
endmodule

module minirv_gpr (
  input  clk_i,
  input  [31:0] wr_data_i,
  input  [4:0] wr_addr_i,
  input  wr_en_i,
  input  [4:0] rd_addr0_i,
  input  [4:0] rd_addr1_i,
  output [31:0] rd_data0_o,
  output [31:0] rd_data1_o
);

  wire and_1_out, and_2_out, decoder_1_out1, decoder_1_out2, decoder_1_out3, decoder_1_out4, decoder_1_out5,
       decoder_1_out6, decoder_1_out7, decoder_1_out8, decoder_1_out9, decoder_1_out10, decoder_1_out11,
       decoder_1_out12, decoder_1_out13, decoder_1_out14, decoder_1_out15, decoder_2_out0, decoder_2_out1,
       decoder_2_out2, decoder_2_out3, decoder_2_out4, decoder_2_out5, decoder_2_out6, decoder_2_out7,
       decoder_2_out8, decoder_2_out9, decoder_2_out10, decoder_2_out11, decoder_2_out12, decoder_2_out13,
       decoder_2_out14, decoder_2_out15;
  wire [31:0] rd_data0_h16, rd_data0_l16, rd_data1_h16, rd_data1_l16, register_1_q, register_2_q,
       register_3_q, register_4_q, register_5_q, register_6_q, register_7_q, register_8_q, register_9_q,
       register_10_q, register_11_q, register_12_q, register_13_q, register_14_q, register_15_q,
       register_16_q, register_17_q, register_18_q, register_19_q, register_20_q, register_21_q,
       register_22_q, register_23_q, register_24_q, register_25_q, register_26_q, register_27_q,
       register_28_q, register_29_q, register_30_q, register_31_q, register_32_q;

  // Probe on wr_data_i
  Decoder #(.select(4)) decoder_1 (
    .out1(decoder_1_out1), .out2(decoder_1_out2), .out3(decoder_1_out3), .out4(decoder_1_out4),
    .out5(decoder_1_out5), .out6(decoder_1_out6), .out7(decoder_1_out7), .out8(decoder_1_out8),
    .out9(decoder_1_out9), .out10(decoder_1_out10), .out11(decoder_1_out11), .out12(decoder_1_out12),
    .out13(decoder_1_out13), .out14(decoder_1_out14), .out15(decoder_1_out15), .sel(wr_addr_i[3:0]),
    .en(and_1_out));  // open: out0
  and and_1 (and_1_out, wr_en_i, ~wr_addr_i[4]);  // AND_Gate
  Decoder #(.select(4)) decoder_2 (
    .out0(decoder_2_out0), .out1(decoder_2_out1), .out2(decoder_2_out2), .out3(decoder_2_out3),
    .out4(decoder_2_out4), .out5(decoder_2_out5), .out6(decoder_2_out6), .out7(decoder_2_out7),
    .out8(decoder_2_out8), .out9(decoder_2_out9), .out10(decoder_2_out10), .out11(decoder_2_out11),
    .out12(decoder_2_out12), .out13(decoder_2_out13), .out14(decoder_2_out14), .out15(decoder_2_out15),
    .sel(wr_addr_i[3:0]), .en(and_2_out));
  and and_2 (and_2_out, wr_en_i, wr_addr_i[4]);
  Register #(.width(32)) register_1 (.D(wr_data_i), .en(1'b0), .clk(clk_i), .Q(register_1_q));  // open: clr
  Register #(.width(32)) register_2 (.D(wr_data_i), .en(decoder_1_out8), .clk(clk_i), .Q(register_2_q));  // open: clr
  Register #(.width(32)) register_3 (.D(wr_data_i), .en(decoder_2_out0), .clk(clk_i), .Q(register_3_q));  // open: clr
  Register #(.width(32)) register_4 (.D(wr_data_i), .en(decoder_2_out8), .clk(clk_i), .Q(register_4_q));  // open: clr
  Register #(.width(32)) register_5 (.D(wr_data_i), .en(decoder_1_out1), .clk(clk_i), .Q(register_5_q));  // open: clr
  Register #(.width(32)) register_6 (.D(wr_data_i), .en(decoder_1_out9), .clk(clk_i), .Q(register_6_q));  // open: clr
  Register #(.width(32)) register_7 (.D(wr_data_i), .en(decoder_2_out1), .clk(clk_i), .Q(register_7_q));  // open: clr
  Register #(.width(32)) register_8 (.D(wr_data_i), .en(decoder_2_out9), .clk(clk_i), .Q(register_8_q));  // open: clr
  Register #(.width(32)) register_9 (.D(wr_data_i), .en(decoder_1_out2), .clk(clk_i), .Q(register_9_q));  // open: clr
  Register #(.width(32)) register_10 (
    .D(wr_data_i), .en(decoder_1_out10), .clk(clk_i), .Q(register_10_q));  // open: clr
  Register #(.width(32)) register_11 (.D(wr_data_i), .en(decoder_2_out2), .clk(clk_i), .Q(register_11_q));  // open: clr
  Register #(.width(32)) register_12 (
    .D(wr_data_i), .en(decoder_2_out10), .clk(clk_i), .Q(register_12_q));  // open: clr
  Register #(.width(32)) register_13 (.D(wr_data_i), .en(decoder_1_out3), .clk(clk_i), .Q(register_13_q));  // open: clr
  Register #(.width(32)) register_14 (
    .D(wr_data_i), .en(decoder_1_out11), .clk(clk_i), .Q(register_14_q));  // open: clr
  Register #(.width(32)) register_15 (.D(wr_data_i), .en(decoder_2_out3), .clk(clk_i), .Q(register_15_q));  // open: clr
  Register #(.width(32)) register_16 (
    .D(wr_data_i), .en(decoder_2_out11), .clk(clk_i), .Q(register_16_q));  // open: clr
  Register #(.width(32)) register_17 (.D(wr_data_i), .en(decoder_1_out4), .clk(clk_i), .Q(register_17_q));  // open: clr
  Register #(.width(32)) register_18 (
    .D(wr_data_i), .en(decoder_1_out12), .clk(clk_i), .Q(register_18_q));  // open: clr
  Register #(.width(32)) register_19 (.D(wr_data_i), .en(decoder_2_out4), .clk(clk_i), .Q(register_19_q));  // open: clr
  Register #(.width(32)) register_20 (
    .D(wr_data_i), .en(decoder_2_out12), .clk(clk_i), .Q(register_20_q));  // open: clr
  Register #(.width(32)) register_21 (.D(wr_data_i), .en(decoder_1_out5), .clk(clk_i), .Q(register_21_q));  // open: clr
  Register #(.width(32)) register_22 (
    .D(wr_data_i), .en(decoder_1_out13), .clk(clk_i), .Q(register_22_q));  // open: clr
  Register #(.width(32)) register_23 (.D(wr_data_i), .en(decoder_2_out5), .clk(clk_i), .Q(register_23_q));  // open: clr
  Register #(.width(32)) register_24 (
    .D(wr_data_i), .en(decoder_2_out13), .clk(clk_i), .Q(register_24_q));  // open: clr
  Register #(.width(32)) register_25 (.D(wr_data_i), .en(decoder_1_out6), .clk(clk_i), .Q(register_25_q));  // open: clr
  Register #(.width(32)) register_26 (
    .D(wr_data_i), .en(decoder_1_out14), .clk(clk_i), .Q(register_26_q));  // open: clr
  Register #(.width(32)) register_27 (.D(wr_data_i), .en(decoder_2_out6), .clk(clk_i), .Q(register_27_q));  // open: clr
  Register #(.width(32)) register_28 (
    .D(wr_data_i), .en(decoder_2_out14), .clk(clk_i), .Q(register_28_q));  // open: clr
  Register #(.width(32)) register_29 (.D(wr_data_i), .en(decoder_1_out7), .clk(clk_i), .Q(register_29_q));  // open: clr
  Register #(.width(32)) register_30 (
    .D(wr_data_i), .en(decoder_1_out15), .clk(clk_i), .Q(register_30_q));  // open: clr
  Register #(.width(32)) register_31 (.D(wr_data_i), .en(decoder_2_out7), .clk(clk_i), .Q(register_31_q));  // open: clr
  Register #(.width(32)) register_32 (
    .D(wr_data_i), .en(decoder_2_out15), .clk(clk_i), .Q(register_32_q));  // open: clr
  Multiplexer #(.select(4), .width(32)) multiplexer_1 (
    .in0(register_1_q), .in1(register_5_q), .in2(register_9_q), .in3(register_13_q), .in4(register_17_q),
    .in5(register_21_q), .in6(register_25_q), .in7(register_29_q), .in8(register_2_q), .in9(register_6_q),
    .in10(register_10_q), .in11(register_14_q), .in12(register_18_q), .in13(register_22_q),
    .in14(register_26_q), .in15(register_30_q), .out(rd_data0_l16), .sel(rd_addr0_i[3:0]));
  Multiplexer #(.select(4), .width(32)) multiplexer_2 (
    .in0(register_1_q), .in1(register_5_q), .in2(register_9_q), .in3(register_13_q), .in4(register_17_q),
    .in5(register_21_q), .in6(register_25_q), .in7(register_29_q), .in8(register_2_q), .in9(register_6_q),
    .in10(register_10_q), .in11(register_14_q), .in12(register_18_q), .in13(register_22_q),
    .in14(register_26_q), .in15(register_30_q), .out(rd_data1_l16), .sel(rd_addr1_i[3:0]));
  Multiplexer #(.select(4), .width(32)) multiplexer_3 (
    .in0(register_3_q), .in1(register_7_q), .in2(register_11_q), .in3(register_15_q), .in4(register_19_q),
    .in5(register_23_q), .in6(register_27_q), .in7(register_31_q), .in8(register_4_q), .in9(register_8_q),
    .in10(register_12_q), .in11(register_16_q), .in12(register_20_q), .in13(register_24_q),
    .in14(register_28_q), .in15(register_32_q), .out(rd_data0_h16), .sel(rd_addr0_i[3:0]));
  Multiplexer #(.select(4), .width(32)) multiplexer_4 (
    .in0(register_3_q), .in1(register_7_q), .in2(register_11_q), .in3(register_15_q), .in4(register_19_q),
    .in5(register_23_q), .in6(register_27_q), .in7(register_31_q), .in8(register_4_q), .in9(register_8_q),
    .in10(register_12_q), .in11(register_16_q), .in12(register_20_q), .in13(register_24_q),
    .in14(register_28_q), .in15(register_32_q), .out(rd_data1_h16), .sel(rd_addr1_i[3:0]));
  Multiplexer #(.width(32)) multiplexer_5 (
    .in0(rd_data0_l16), .in1(rd_data0_h16), .out(rd_data0_o), .sel(rd_addr0_i[4]));
  Multiplexer #(.width(32)) multiplexer_6 (
    .in0(rd_data1_l16), .in1(rd_data1_h16), .out(rd_data1_o), .sel(rd_addr1_i[4]));

  // Other names for the same wires on the sheet: rd_addr0_lb[3:0] = rd_addr0_i[3:0]; rd_addr0_hb = rd_addr0_i[4];
  //   rd_addr1_lb[3:0] = rd_addr1_i[3:0]; rd_addr1_hb = rd_addr1_i[4]; rd_data0[31:0] = rd_data0_o;
  //   rd_data1[31:0] = rd_data1_o; wr_addr_lb[3:0] = wr_addr_i[3:0]; wr_addr_hb = wr_addr_i[4];
  //   wr_data[31:0] = wr_data_i; wr_en = wr_en_i
endmodule

module minirv_alu (
  input  [31:0] imm_i,
  input  [31:0] data0_i,
  input  [31:0] data1_i,
  input  is_add_i,
  input  is_addi_i,
  input  is_lui_i,
  input  is_lw_i,
  input  is_lbu_i,
  input  is_sw_i,
  input  is_sb_i,
  input  is_jalr_i,
  output [31:0] data_o
);

  wire [2:0] sel;
  wire [31:0] add_val, adder_3_out, addi_val, jalr_val;

  Adder #(.width(32)) adder_1 (.a(data0_i), .b(data1_i), .out(add_val));  // open: cin, cout
  Adder #(.width(32)) adder_2 (.a(data0_i), .b(imm_i), .out(addi_val));  // open: cin, cout
  Adder #(.width(32)) adder_3 (.a(data0_i), .b(imm_i), .out(adder_3_out));  // open: cin, cout
  assign jalr_val = adder_3_out & 32'hfffffffe;  // AND_Gate and_1, 32 bits wide
  Multiplexer #(.select(3), .width(32)) multiplexer_1 (
    .in0(add_val), .in1(addi_val), .in2(imm_i), .in3(addi_val), .in4(addi_val), .in5(addi_val),
    .in6(addi_val), .in7(jalr_val), .out(data_o), .sel(sel));
  Priority_Encoder priority_encoder_1 (
    .in0(is_add_i), .in1(is_addi_i), .in2(is_lui_i), .in3(is_lw_i), .in4(is_lbu_i), .in5(is_sw_i),
    .in6(is_sb_i), .in7(is_jalr_i), .out(sel));  // open: en_in, gs, en_out
  // Probe on sel

  // Other names for the same wires on the sheet: data0[31:0] = data0_i; data1[31:0] = data1_i; is_add = is_add_i;
  //   is_addi = is_addi_i; is_jalr = is_jalr_i; is_lbu = is_lbu_i; is_lui = is_lui_i; is_lw = is_lw_i;
  //   is_sb = is_sb_i; is_sw = is_sw_i; imm[31:0] = imm_i; lui_val[31:0] = imm_i; lbu_val[31:0] = addi_val;
  //   lw_val[31:0] = addi_val; sb_val[31:0] = addi_val; sw_val[31:0] = addi_val; val_sel[31:0] = data_o

  // Notes on the sheet:
  //   Copyright (c) 2026 Guiyuan Zhu. All rights reserved.
endmodule

module minirv_pc (
  input  clk_i,
  input  rst_i,
  input  load_en_i,
  input  [31:0] load_data_i,
  output [31:0] pc_o,
  output [31:0] pc_nxt_o,
  output [31:0] perf_o
);

  wire [31:0] multiplexer_1_out, register_2_q;

  Register #(.width(32)) register_1 (.D(multiplexer_1_out), .en(1'b1), .clk(clk_i), .Q(pc_o), .clr(rst_i));
  Multiplexer #(.width(32)) multiplexer_1 (.in0(pc_nxt_o), .in1(load_data_i), .out(multiplexer_1_out), .sel(load_en_i));
  Register #(.width(32)) register_2 (.D(perf_o), .en(1'b1), .clk(clk_i), .Q(register_2_q), .clr(rst_i));
  Adder #(.width(32)) adder_1 (.a(pc_o), .b(32'h4), .out(pc_nxt_o));  // open: cin, cout
  Adder #(.width(32)) adder_2 (.a(register_2_q), .b(32'h1), .out(perf_o));  // open: cin, cout

  // Notes on the sheet:
  //   Copyright (c) 2026 Guiyuan Zhu. All rights reserved.
endmodule

module minirv_gpr_rd_driver (
  input  [31:0] alu_result_i,
  input  [31:0] pc_nxt_i,
  input  [31:0] mem_data_i,
  input  is_add_i,
  input  is_addi_i,
  input  is_lui_i,
  input  is_lw_i,
  input  is_lbu_i,
  input  is_sw_i,
  input  is_sb_i,
  input  is_jalr_i,
  output [31:0] rd_val_o,
  output rd_wr_en_o
);

  wire rd_from_alu, rd_from_mem;
  wire [31:0] multiplexer_1_out;

  or or_1 (rd_wr_en_o, is_add_i, is_addi_i, is_lui_i, is_lw_i, is_lbu_i, is_jalr_i);
  or or_2 (rd_from_alu, is_add_i, is_addi_i, is_lui_i);
  or or_3 (rd_from_mem, is_lw_i, is_lbu_i);
  Multiplexer #(.width(32)) multiplexer_1 (
    .in0(alu_result_i), .in1(mem_data_i), .out(multiplexer_1_out), .sel(rd_from_mem));
  Multiplexer #(.width(32)) multiplexer_2 (.in0(multiplexer_1_out), .in1(pc_nxt_i), .out(rd_val_o), .sel(is_jalr_i));

  // Other names for the same wires on the sheet: alu_result[31:0] = alu_result_i; is_add = is_add_i;
  //   is_addi = is_addi_i; is_lbu = is_lbu_i; is_lui = is_lui_i; is_lw = is_lw_i; is_sb = is_sb_i; is_sw = is_sw_i;
  //   mem_data[31:0] = mem_data_i; pc_nxt[31:0] = pc_nxt_i; is_jalr = is_jalr_i; rd_from_pc = is_jalr_i;
  //   rd_wr_en = rd_wr_en_o; val_sel[31:0] = rd_val_o

  // Notes on the sheet:
  //   Copyright (c) 2026 Guiyuan Zhu. All rights reserved.
endmodule

module minirv_mem_driver (
  input  [31:0] alu_result_i,
  input  [31:0] rs2_val_i,
  input  is_lw_i,
  input  is_lbu_i,
  input  is_sw_i,
  input  is_sb_i,
  input  [31:0] mem_rd_data_i,
  output [31:0] mem_addr_o,
  output mem_wr_en_o,
  output [3:0] mem_wr_mask_o,
  output [31:0] mem_wr_data_o,
  output [31:0] mem_rd_data_o
);

  wire [3:0] multiplexer_1_out, sb_mask;
  wire [7:0] multiplexer_4_out;
  wire [31:0] bit_extender_1_out;

  Multiplexer #(.width(4)) multiplexer_1 (.in0(4'b0000), .in1(4'b1111), .out(multiplexer_1_out), .sel(is_sw_i));
  or or_1 (mem_wr_en_o, is_sw_i, is_sb_i);
  Multiplexer #(.width(32)) multiplexer_2 (
    .in0(rs2_val_i), .in1({rs2_val_i[7:0], rs2_val_i[7:0], rs2_val_i[7:0], rs2_val_i[7:0]}),
    .out(mem_wr_data_o), .sel(is_sb_i));
  Multiplexer #(.width(4)) multiplexer_3 (.in0(multiplexer_1_out), .in1(sb_mask), .out(mem_wr_mask_o), .sel(is_sb_i));
  Multiplexer #(.select(2), .width(8)) multiplexer_4 (
    .in0(mem_rd_data_i[7:0]), .in1(mem_rd_data_i[15:8]), .in2(mem_rd_data_i[23:16]),
    .in3(mem_rd_data_i[31:24]), .out(multiplexer_4_out), .sel(alu_result_i[1:0]));
  assign bit_extender_1_out = {{24{1'b0}}, multiplexer_4_out};  // Bit_Extender bit_extender_1
  Multiplexer #(.select(2), .width(4)) multiplexer_5 (
    .in0(4'b0001), .in1(4'b0010), .in2(4'b0100), .in3(4'b1000), .out(sb_mask), .sel(alu_result_i[1:0]));
  Multiplexer #(.width(32)) multiplexer_6 (
    .in0(mem_rd_data_i), .in1(bit_extender_1_out), .out(mem_rd_data_o), .sel(is_lbu_i));

  assign mem_addr_o = alu_result_i;

  // Other names for the same wires on the sheet: is_lbu = is_lbu_i; is_lw = is_lw_i; is_sb = is_sb_i; is_sw = is_sw_i;
  //   alu_result[31:0] = alu_result_i; mem_addr[31:0] = alu_result_i; mem_rd_data[31:0] = mem_rd_data_o;
  //   mem_rd_data_raw[31:0] = mem_rd_data_i; mem_wr_data[31:0] = mem_wr_data_o; mem_wr_en = mem_wr_en_o;
  //   mem_wr_mask[3:0] = mem_wr_mask_o; rs2_val[31:0] = rs2_val_i

  // Notes on the sheet:
  //   Copyright (c) 2026 Guiyuan Zhu. All rights reserved.
endmodule
