// Logisim project f_2607.circ as structural Verilog: 74 circuits, main circuit main
module main (
);


  // Notes on the sheet:
  //   Copyright (c) 2026 Guiyuan Zhu. All rights reserved.
endmodule

module decoder_2_4 (
  input  [1:0] data_i,
  output [3:0] data_o
);

  and and_1 (data_o[0], ~data_i[0], ~data_i[1]);  // AND_Gate
  and and_2 (data_o[1], data_i[0], ~data_i[1]);  // AND_Gate
  and and_3 (data_o[2], ~data_i[0], data_i[1]);  // AND_Gate
  and and_4 (data_o[3], data_i[0], data_i[1]);

  // Notes on the sheet:
  //   Copyright (c) 2026 Guiyuan Zhu. All rights reserved.
endmodule

module decoder_3_8 (
  input  [2:0] data_i,
  output [7:0] data_o
);

  wire [3:0] bit_extender_1_out, decoder_2_4_1_data_o, decoder_2_4_2_data_o;

  assign bit_extender_1_out = {{3{data_i[2]}}, data_i[2]};  // Bit_Extender bit_extender_1
  decoder_2_4 decoder_2_4_1 (.data_i(data_i[1:0]), .data_o(decoder_2_4_1_data_o));
  decoder_2_4 decoder_2_4_2 (.data_i(data_i[1:0]), .data_o(decoder_2_4_2_data_o));
  // Probe on bit_extender_1_out
  assign data_o[3:0] = decoder_2_4_1_data_o & ~bit_extender_1_out;  // AND_Gate and_1, 4 bits wide
  assign data_o[7:4] = decoder_2_4_2_data_o & bit_extender_1_out;  // AND_Gate and_2, 4 bits wide

  // Notes on the sheet:
  //   Copyright (c) 2026 Guiyuan Zhu. All rights reserved.
endmodule

module decoder_4_16 (
  input  [3:0] data_i,
  output [15:0] data_o
);

  wire [7:0] bit_extender_1_out, decoder_3_8_1_data_o, decoder_3_8_2_data_o;

  assign bit_extender_1_out = {{7{data_i[3]}}, data_i[3]};  // Bit_Extender bit_extender_1
  decoder_3_8 decoder_3_8_1 (.data_i(data_i[2:0]), .data_o(decoder_3_8_1_data_o));
  decoder_3_8 decoder_3_8_2 (.data_i(data_i[2:0]), .data_o(decoder_3_8_2_data_o));
  // Probe on bit_extender_1_out
  assign data_o[7:0] = decoder_3_8_1_data_o & ~bit_extender_1_out;  // AND_Gate and_1, 8 bits wide
  assign data_o[15:8] = decoder_3_8_2_data_o & bit_extender_1_out;  // AND_Gate and_2, 8 bits wide

  // Notes on the sheet:
  //   Copyright (c) 2026 Guiyuan Zhu. All rights reserved.
endmodule

module segment_3_7_v1 (
  input  [3:0] data_i,
  output a_o,
  output b_o,
  output c_o,
  output d_o,
  output e_o,
  output f_o,
  output g_o,
  output h_o
);

  wire [15:0] decoder_4_16_1_data_o;

  _7_Segment_Display u_7_segment_display_1 (.g(g_o), .f(f_o), .a(a_o), .b(b_o), .e(e_o), .d(d_o), .c(c_o), .dp(h_o));
  decoder_4_16 decoder_4_16_1 (.data_i(data_i), .data_o(decoder_4_16_1_data_o));
  or or_1 (a_o, decoder_4_16_1_data_o[0], decoder_4_16_1_data_o[2], decoder_4_16_1_data_o[3], decoder_4_16_1_data_o[5], decoder_4_16_1_data_o[6], decoder_4_16_1_data_o[7], decoder_4_16_1_data_o[8], decoder_4_16_1_data_o[9]);
  or or_2 (b_o, decoder_4_16_1_data_o[0], decoder_4_16_1_data_o[1], decoder_4_16_1_data_o[2], decoder_4_16_1_data_o[3], decoder_4_16_1_data_o[4], decoder_4_16_1_data_o[7], decoder_4_16_1_data_o[8], decoder_4_16_1_data_o[9]);
  or or_3 (c_o, decoder_4_16_1_data_o[0], decoder_4_16_1_data_o[1], decoder_4_16_1_data_o[3], decoder_4_16_1_data_o[4], decoder_4_16_1_data_o[5], decoder_4_16_1_data_o[6], decoder_4_16_1_data_o[7], decoder_4_16_1_data_o[8], decoder_4_16_1_data_o[9]);
  or or_4 (d_o, decoder_4_16_1_data_o[0], decoder_4_16_1_data_o[2], decoder_4_16_1_data_o[3], decoder_4_16_1_data_o[5], decoder_4_16_1_data_o[6], decoder_4_16_1_data_o[8], decoder_4_16_1_data_o[9]);
  or or_5 (e_o, decoder_4_16_1_data_o[0], decoder_4_16_1_data_o[2], decoder_4_16_1_data_o[6], decoder_4_16_1_data_o[8]);
  or or_6 (f_o, decoder_4_16_1_data_o[0], decoder_4_16_1_data_o[4], decoder_4_16_1_data_o[5], decoder_4_16_1_data_o[6], decoder_4_16_1_data_o[8], decoder_4_16_1_data_o[9]);
  or or_7 (g_o, decoder_4_16_1_data_o[2], decoder_4_16_1_data_o[3], decoder_4_16_1_data_o[4], decoder_4_16_1_data_o[5], decoder_4_16_1_data_o[6], decoder_4_16_1_data_o[8], decoder_4_16_1_data_o[9]);
  or or_8 (h_o, decoder_4_16_1_data_o[10], decoder_4_16_1_data_o[11], decoder_4_16_1_data_o[12], decoder_4_16_1_data_o[13], decoder_4_16_1_data_o[14], decoder_4_16_1_data_o[15]);

  // Other names for the same wires on the sheet: a = a_o; b = b_o; c = c_o; d = d_o; e = e_o; f = f_o; g = g_o;
  //   h = h_o

  // Notes on the sheet:
  //   Copyright (c) 2026 Guiyuan Zhu. All rights reserved.
endmodule

module segment_3_7_v2 (
  input  [3:0] data_i,
  output a_o,
  output b_o,
  output c_o,
  output d_o,
  output e_o,
  output f_o,
  output g_o,
  output h_o
);

  wire [15:0] decoder_4_16_1_data_o;

  _7_Segment_Display u_7_segment_display_1 (.g(g_o), .f(f_o), .a(a_o), .b(b_o), .e(e_o), .d(d_o), .c(c_o), .dp(1'b0));
  decoder_4_16 decoder_4_16_1 (.data_i(data_i), .data_o(decoder_4_16_1_data_o));
  or or_1 (a_o, decoder_4_16_1_data_o[0], decoder_4_16_1_data_o[2], decoder_4_16_1_data_o[3], decoder_4_16_1_data_o[5], decoder_4_16_1_data_o[6], decoder_4_16_1_data_o[7], decoder_4_16_1_data_o[8], decoder_4_16_1_data_o[9], decoder_4_16_1_data_o[10], decoder_4_16_1_data_o[12], decoder_4_16_1_data_o[14], decoder_4_16_1_data_o[15]);
  or or_2 (b_o, decoder_4_16_1_data_o[0], decoder_4_16_1_data_o[1], decoder_4_16_1_data_o[2], decoder_4_16_1_data_o[3], decoder_4_16_1_data_o[4], decoder_4_16_1_data_o[7], decoder_4_16_1_data_o[8], decoder_4_16_1_data_o[9], decoder_4_16_1_data_o[10], decoder_4_16_1_data_o[13]);
  or or_3 (c_o, decoder_4_16_1_data_o[0], decoder_4_16_1_data_o[1], decoder_4_16_1_data_o[3], decoder_4_16_1_data_o[4], decoder_4_16_1_data_o[5], decoder_4_16_1_data_o[6], decoder_4_16_1_data_o[7], decoder_4_16_1_data_o[8], decoder_4_16_1_data_o[9], decoder_4_16_1_data_o[10], decoder_4_16_1_data_o[11], decoder_4_16_1_data_o[13]);
  or or_4 (d_o, decoder_4_16_1_data_o[0], decoder_4_16_1_data_o[2], decoder_4_16_1_data_o[3], decoder_4_16_1_data_o[5], decoder_4_16_1_data_o[6], decoder_4_16_1_data_o[8], decoder_4_16_1_data_o[9], decoder_4_16_1_data_o[11], decoder_4_16_1_data_o[12], decoder_4_16_1_data_o[13], decoder_4_16_1_data_o[14]);
  or or_5 (e_o, decoder_4_16_1_data_o[0], decoder_4_16_1_data_o[2], decoder_4_16_1_data_o[6], decoder_4_16_1_data_o[8], decoder_4_16_1_data_o[10], decoder_4_16_1_data_o[11], decoder_4_16_1_data_o[12], decoder_4_16_1_data_o[13], decoder_4_16_1_data_o[14], decoder_4_16_1_data_o[15]);
  or or_6 (f_o, decoder_4_16_1_data_o[0], decoder_4_16_1_data_o[4], decoder_4_16_1_data_o[5], decoder_4_16_1_data_o[6], decoder_4_16_1_data_o[8], decoder_4_16_1_data_o[9], decoder_4_16_1_data_o[10], decoder_4_16_1_data_o[11], decoder_4_16_1_data_o[12], decoder_4_16_1_data_o[14], decoder_4_16_1_data_o[15]);
  or or_7 (g_o, decoder_4_16_1_data_o[2], decoder_4_16_1_data_o[3], decoder_4_16_1_data_o[4], decoder_4_16_1_data_o[5], decoder_4_16_1_data_o[6], decoder_4_16_1_data_o[8], decoder_4_16_1_data_o[9], decoder_4_16_1_data_o[10], decoder_4_16_1_data_o[11], decoder_4_16_1_data_o[13], decoder_4_16_1_data_o[14], decoder_4_16_1_data_o[15]);

  assign h_o = 1'b0;

  // Other names for the same wires on the sheet: a = a_o; b = b_o; c = c_o; d = d_o; e = e_o; f = f_o; g = g_o

  // Notes on the sheet:
  //   Copyright (c) 2026 Guiyuan Zhu. All rights reserved.
endmodule

module encoder_4_2 (
  input  [3:0] data_i,
  output [1:0] data_o
);

  or or_1 (data_o[0], data_i[1], data_i[3]);
  or or_2 (data_o[1], data_i[2], data_i[3]);

  // Notes on the sheet:
  //   Copyright (c) 2026 Guiyuan Zhu. All rights reserved.
endmodule

module encoder_16_4 (
  input  [15:0] data_i,
  output [3:0] data_o
);

  or or_1 (data_o[0], data_i[1], data_i[3], data_i[5], data_i[7], data_i[9], data_i[11], data_i[13], data_i[15]);
  or or_2 (data_o[1], data_i[2], data_i[3], data_i[6], data_i[7], data_i[10], data_i[11], data_i[14], data_i[15]);
  or or_3 (data_o[2], data_i[4], data_i[5], data_i[6], data_i[7], data_i[12], data_i[13], data_i[14], data_i[15]);
  or or_4 (data_o[3], data_i[8], data_i[9], data_i[10], data_i[11], data_i[12], data_i[13], data_i[14], data_i[15]);

  // Notes on the sheet:
  //   Copyright (c) 2026 Guiyuan Zhu. All rights reserved.
endmodule

module encoder_top (
  input  [15:0] data_i
);

  wire a, b, c, d, e, f, g, h;
  wire [3:0] encoder_16_4_1_data_o;

  _7_Segment_Display u_7_segment_display_1 (.g(g), .f(f), .a(a), .b(b), .e(e), .d(d), .c(c), .dp(h));
  encoder_16_4 encoder_16_4_1 (.data_i(data_i), .data_o(encoder_16_4_1_data_o));
  segment_3_7_v2 segment_3_7_v2_1 (
    .data_i(encoder_16_4_1_data_o), .a_o(a), .b_o(b), .c_o(c), .d_o(d), .e_o(e), .f_o(f), .g_o(g), .h_o(h));

  // Notes on the sheet:
  //   Copyright (c) 2026 Guiyuan Zhu. All rights reserved.
endmodule

module priority_encoder_4_2 (
  input  [3:0] data_i,
  input  en_i,
  output [1:0] data_o
);

  wire and_1_out, and_2_out;
  wire [1:0] bit_extender_1_out, or_1_out;

  assign bit_extender_1_out = {{1{en_i}}, en_i};  // Bit_Extender bit_extender_1
  and and_1 (and_1_out, data_i[1], ~data_i[2], ~data_i[3]);  // AND_Gate
  or or_1 (or_1_out[0], and_1_out, data_i[3]);
  and and_2 (and_2_out, data_i[2], ~data_i[3]);  // AND_Gate
  or or_2 (or_1_out[1], and_2_out, data_i[3]);
  assign data_o = or_1_out & bit_extender_1_out;  // AND_Gate and_3, 2 bits wide

  // Notes on the sheet:
  //   Copyright (c) 2026 Guiyuan Zhu. All rights reserved.
endmodule

module priority_encoder_16_4 (
  input  [15:0] data_i,
  input  en_i,
  output [3:0] data_o
);

  wire and_1_out, and_2_out, not_1_out;
  wire [1:0] or_5_out, priority_encoder_4_2_1_data_o, priority_encoder_4_2_2_data_o,
       priority_encoder_4_2_3_data_o, priority_encoder_4_2_4_data_o;
  wire [3:0] bit_extender_1_out, or_1_out;
  wire [3:2] priority_encoder_4_2_5_data_o;

  or or_1 (or_1_out[0], data_i[0], data_i[1], data_i[2], data_i[3]);
  or or_2 (or_1_out[1], data_i[4], data_i[5], data_i[6], data_i[7]);
  or or_3 (or_1_out[2], data_i[8], data_i[9], data_i[10], data_i[11]);
  or or_4 (or_1_out[3], data_i[12], data_i[13], data_i[14], data_i[15]);
  and and_1 (and_1_out, ~or_1_out[1], ~or_1_out[2], ~or_1_out[3]);  // AND_Gate
  and and_2 (and_2_out, ~or_1_out[2], ~or_1_out[3]);  // AND_Gate
  not not_1 (not_1_out, or_1_out[3]);
  assign bit_extender_1_out = {{3{en_i}}, en_i};  // Bit_Extender bit_extender_1
  priority_encoder_4_2 priority_encoder_4_2_1 (
    .data_i(data_i[3:0]), .en_i(and_1_out), .data_o(priority_encoder_4_2_1_data_o));
  priority_encoder_4_2 priority_encoder_4_2_2 (
    .data_i(data_i[7:4]), .en_i(and_2_out), .data_o(priority_encoder_4_2_2_data_o));
  priority_encoder_4_2 priority_encoder_4_2_3 (
    .data_i(data_i[11:8]), .en_i(not_1_out), .data_o(priority_encoder_4_2_3_data_o));
  priority_encoder_4_2 priority_encoder_4_2_4 (
    .data_i(data_i[15:12]), .en_i(1'b1), .data_o(priority_encoder_4_2_4_data_o));
  priority_encoder_4_2 priority_encoder_4_2_5 (.data_i(or_1_out), .en_i(1'b1), .data_o(priority_encoder_4_2_5_data_o));
  assign or_5_out = priority_encoder_4_2_1_data_o | priority_encoder_4_2_2_data_o | priority_encoder_4_2_3_data_o | priority_encoder_4_2_4_data_o;  // OR_Gate or_5, 2 bits wide
  assign data_o = {priority_encoder_4_2_5_data_o, or_5_out} & bit_extender_1_out;  // AND_Gate and_3, 4 bits wide

  // Notes on the sheet:
  //   前导 0 的数目是优先编码器的结果取反
  //   尾随 0 则输入 bit swap 之后按照上述算法计算  
  //   全 0 和全 1 需要单独归并检测
  //   前导 1 则取反之后按照上述算法计算
  //   前导 0 则输入 bit swap 并取反之后按照上述算法计算
  //   Copyright (c) 2026 Guiyuan Zhu. All rights reserved.
endmodule

module mux2_1b_v1 (
  input  sel_i,
  input  a_i,
  input  b_i,
  output c_o
);

  wire transistor_1_out;

  Transistor transistor_1 (.in(1'b1), .out(transistor_1_out), .gate(sel_i));
  Transistor #(.\type ("n")) transistor_2 (.in(1'b0), .out(transistor_1_out), .gate(sel_i));
  // Transmission_Gate transmission_1: pin names not known; wires that end beside it: a_i, sel_i, transistor_1_out, c_o
  // Transmission_Gate transmission_2: pin names not known; wires that end beside it: c_o, sel_i, transistor_1_out, b_i

  // Notes on the sheet:
  //   Copyright (c) 2026 Guiyuan Zhu. All rights reserved.
endmodule

module mux2_1b_v2 (
  input  sel_i,
  input  a_i,
  input  b_i,
  output c_o
);

  wire and_1_out, and_2_out;

  and and_1 (and_1_out, ~sel_i, a_i);  // AND_Gate
  and and_2 (and_2_out, sel_i, b_i);
  or or_1 (c_o, and_1_out, and_2_out);

  // Notes on the sheet:
  //   Copyright (c) 2026 Guiyuan Zhu. All rights reserved.
endmodule

module mux4_3b_v1 (
  input  [1:0] sel_i,
  input  [2:0] a_i,
  input  [2:0] b_i,
  input  [2:0] c_i,
  input  [2:0] d_i,
  output [2:0] e_o
);

  wire [2:0] multiplexer_1_out, multiplexer_2_out;

  Multiplexer #(.width(3)) multiplexer_1 (.in0(a_i), .in1(b_i), .out(multiplexer_1_out), .sel(sel_i[0]));
  Multiplexer #(.width(3)) multiplexer_2 (.in0(c_i), .in1(d_i), .out(multiplexer_2_out), .sel(sel_i[0]));
  Multiplexer #(.width(3)) multiplexer_3 (.in0(multiplexer_1_out), .in1(multiplexer_2_out), .out(e_o), .sel(sel_i[1]));

  // Notes on the sheet:
  //   Copyright (c) 2026 Guiyuan Zhu. All rights reserved.
endmodule

module mux4_3b_v2 (
  input  [1:0] sel_i,
  input  [2:0] a_i,
  input  [2:0] b_i,
  input  [2:0] c_i,
  input  [2:0] d_i,
  output [2:0] e_o
);

  wire [2:0] and_1_out, and_2_out, and_3_out, and_4_out, bit_extender_1_out, bit_extender_2_out,
       bit_extender_3_out, bit_extender_4_out;
  wire [3:0] decoder_2_4_1_data_o;

  decoder_2_4 decoder_2_4_1 (.data_i(sel_i), .data_o(decoder_2_4_1_data_o));
  assign bit_extender_1_out = {{2{decoder_2_4_1_data_o[0]}}, decoder_2_4_1_data_o[0]};  // Bit_Extender bit_extender_1
  assign bit_extender_2_out = {{2{decoder_2_4_1_data_o[1]}}, decoder_2_4_1_data_o[1]};  // Bit_Extender bit_extender_2
  assign bit_extender_3_out = {{2{decoder_2_4_1_data_o[2]}}, decoder_2_4_1_data_o[2]};  // Bit_Extender bit_extender_3
  assign bit_extender_4_out = {{2{decoder_2_4_1_data_o[3]}}, decoder_2_4_1_data_o[3]};  // Bit_Extender bit_extender_4
  assign and_1_out = bit_extender_1_out & a_i;  // AND_Gate and_1, 3 bits wide
  assign and_2_out = bit_extender_2_out & b_i;  // AND_Gate and_2, 3 bits wide
  assign and_3_out = bit_extender_3_out & c_i;  // AND_Gate and_3, 3 bits wide
  assign and_4_out = bit_extender_4_out & d_i;  // AND_Gate and_4, 3 bits wide
  assign e_o = and_1_out | and_2_out | and_3_out | and_4_out;  // OR_Gate or_1, 3 bits wide

  // Notes on the sheet:
  //   Copyright (c) 2026 Guiyuan Zhu. All rights reserved.
endmodule

module segment_mux (
  input  [3:0] data_i,
  input  dec_i
);

  wire a, a_0, a_1, b, b_0, b_1, c, c_0, c_1, d, d_0, d_1, e, e_0, e_1, f, f_0, f_1, g, g_0, g_1, h, h_0,
       h_1, sel;

  not not_1 (sel, dec_i);
  _7_Segment_Display u_7_segment_display_1 (.g(g), .f(f), .a(a), .b(b), .e(e), .d(d), .c(c), .dp(h));
  segment_3_7_v1 segment_3_7_v1_1 (
    .data_i(data_i), .a_o(a_0), .b_o(b_0), .c_o(c_0), .d_o(d_0), .e_o(e_0), .f_o(f_0), .g_o(g_0), .h_o(h_0));
  segment_3_7_v2 segment_3_7_v2_1 (
    .data_i(data_i), .a_o(a_1), .b_o(b_1), .c_o(c_1), .d_o(d_1), .e_o(e_1), .f_o(f_1), .g_o(g_1), .h_o(h_1));
  mux2_1b_v1 mux2_1b_v1_1 (.sel_i(sel), .a_i(a_0), .b_i(a_1), .c_o(a));
  mux2_1b_v1 mux2_1b_v1_2 (.sel_i(sel), .a_i(b_0), .b_i(b_1), .c_o(b));
  mux2_1b_v1 mux2_1b_v1_3 (.sel_i(sel), .a_i(c_0), .b_i(c_1), .c_o(c));
  mux2_1b_v1 mux2_1b_v1_4 (.sel_i(sel), .a_i(d_0), .b_i(d_1), .c_o(d));
  mux2_1b_v1 mux2_1b_v1_5 (.sel_i(sel), .a_i(e_0), .b_i(e_1), .c_o(e));
  mux2_1b_v1 mux2_1b_v1_6 (.sel_i(sel), .a_i(f_0), .b_i(f_1), .c_o(f));
  mux2_1b_v1 mux2_1b_v1_7 (.sel_i(sel), .a_i(g_0), .b_i(g_1), .c_o(g));
  mux2_1b_v1 mux2_1b_v1_8 (.sel_i(sel), .a_i(h_0), .b_i(h_1), .c_o(h));

  // Notes on the sheet:
  //   Copyright (c) 2026 Guiyuan Zhu. All rights reserved.
endmodule

module comparator_4b (
);

  wire dipswitch_1_sw1, dipswitch_1_sw2, dipswitch_1_sw3, dipswitch_1_sw4, dipswitch_2_sw1, dipswitch_2_sw2,
       dipswitch_2_sw3, dipswitch_2_sw4, nor_1_out, xor_1_out, xor_2_out, xor_3_out, xor_4_out;

  DipSwitch #(.number(4)) dipswitch_1 (
    .sw1(dipswitch_1_sw1), .sw2(dipswitch_1_sw2), .sw3(dipswitch_1_sw3), .sw4(dipswitch_1_sw4));
  DipSwitch #(.number(4)) dipswitch_2 (
    .sw1(dipswitch_2_sw1), .sw2(dipswitch_2_sw2), .sw3(dipswitch_2_sw3), .sw4(dipswitch_2_sw4));
  xor xor_1 (xor_1_out, dipswitch_1_sw1, dipswitch_2_sw1);
  xor xor_2 (xor_2_out, dipswitch_1_sw2, dipswitch_2_sw2);
  xor xor_3 (xor_3_out, dipswitch_1_sw3, dipswitch_2_sw3);
  xor xor_4 (xor_4_out, dipswitch_1_sw4, dipswitch_2_sw4);
  nor nor_1 (nor_1_out, xor_1_out, xor_2_out, xor_3_out, xor_4_out);
  LED led_1 (.in(nor_1_out));

  // Notes on the sheet:
  //   Copyright (c) 2026 Guiyuan Zhu. All rights reserved.
endmodule

module half_adder_1b (
  input  a_i,
  input  b_i,
  output sum_o,
  output cout_o
);

  xor xor_1 (sum_o, a_i, b_i);
  and and_1 (cout_o, a_i, b_i);

  // Notes on the sheet:
  //   Copyright (c) 2026 Guiyuan Zhu. All rights reserved.
endmodule

module full_adder_1b_v1 (
  input  cin_i,
  input  a_i,
  input  b_i,
  output sum_o,
  output cout_o
);

  wire half_adder_1b_1_cout_o, half_adder_1b_2_cout_o, half_adder_1b_2_sum_o;

  half_adder_1b half_adder_1b_1 (
    .a_i(half_adder_1b_2_sum_o), .b_i(cin_i), .sum_o(sum_o), .cout_o(half_adder_1b_1_cout_o));
  half_adder_1b half_adder_1b_2 (.a_i(a_i), .b_i(b_i), .sum_o(half_adder_1b_2_sum_o), .cout_o(half_adder_1b_2_cout_o));
  or or_1 (cout_o, half_adder_1b_1_cout_o, half_adder_1b_2_cout_o);

  // Notes on the sheet:
  //   Copyright (c) 2026 Guiyuan Zhu. All rights reserved.
endmodule

module full_adder_1b_v2 (
  input  cin_i,
  input  a_i,
  input  b_i,
  output sum_o,
  output cout_o
);

  wire and_1_out, and_2_out, xor_1_out;

  xor xor_1 (xor_1_out, a_i, b_i);
  and and_1 (and_1_out, a_i, b_i);
  and and_2 (and_2_out, xor_1_out, cin_i);
  xor xor_2 (sum_o, xor_1_out, cin_i);
  or or_1 (cout_o, and_1_out, and_2_out);

  // Notes on the sheet:
  //   Copyright (c) 2026 Guiyuan Zhu. All rights reserved.
endmodule

module rca_4b_raw (
  input  cin_i,
  input  [3:0] a_i,
  input  [3:0] b_i,
  output [3:0] sum_o,
  output cout_o
);

  wire full_adder_1b_v2_1_cout_o, full_adder_1b_v2_2_cout_o, full_adder_1b_v2_3_cout_o;

  full_adder_1b_v2 full_adder_1b_v2_1 (
    .cin_i(cin_i), .a_i(a_i[0]), .b_i(b_i[0]), .sum_o(sum_o[0]), .cout_o(full_adder_1b_v2_1_cout_o));
  full_adder_1b_v2 full_adder_1b_v2_2 (
    .cin_i(full_adder_1b_v2_1_cout_o), .a_i(a_i[1]), .b_i(b_i[1]), .sum_o(sum_o[1]),
    .cout_o(full_adder_1b_v2_2_cout_o));
  full_adder_1b_v2 full_adder_1b_v2_3 (
    .cin_i(full_adder_1b_v2_2_cout_o), .a_i(a_i[2]), .b_i(b_i[2]), .sum_o(sum_o[2]),
    .cout_o(full_adder_1b_v2_3_cout_o));
  full_adder_1b_v2 full_adder_1b_v2_4 (
    .cin_i(full_adder_1b_v2_3_cout_o), .a_i(a_i[3]), .b_i(b_i[3]), .sum_o(sum_o[3]), .cout_o(cout_o));

  // Notes on the sheet:
  //   Copyright (c) 2026 Guiyuan Zhu. All rights reserved.
endmodule

module adder_top (
  input  [3:0] a_i,
  input  [3:0] b_i
);

  wire cout;
  wire [3:0] sum;

  segment_mux segment_mux_1 (.data_i(a_i));  // open: dec_i
  segment_mux segment_mux_2 (.data_i(sum));  // open: dec_i
  segment_mux segment_mux_3 (.data_i(b_i));  // open: dec_i
  LED led_1 (.in(cout));
  rca_4b_raw rca_4b_raw_1 (.cin_i(1'b0), .a_i(a_i), .b_i(b_i), .sum_o(sum), .cout_o(cout));

  // Other names for the same wires on the sheet: a[3:0] = a_i; b[3:0] = b_i

  // Notes on the sheet:
  //   Copyright (c) 2026 Guiyuan Zhu. All rights reserved.
endmodule

module sr_latch (
  input  r_i,
  input  s_i,
  output q_o,
  output q_no
);

  nor nor_1 (q_o, r_i, q_no);
  nor nor_2 (q_no, q_o, s_i);

  // Notes on the sheet:
  //   Copyright (c) 2026 Guiyuan Zhu. All rights reserved.
endmodule

module snrn_latch (
  input  r_ni,
  input  s_ni,
  output q_o,
  output q_no
);

  nand nand_1 (q_o, r_ni, q_no);
  nand nand_2 (q_no, q_o, s_ni);

  // Notes on the sheet:
  //   Copyright (c) 2026 Guiyuan Zhu. All rights reserved.
endmodule

module d_latch (
  input  we_i,
  input  d_i,
  output q_o,
  output q_no
);

  wire and_1_out, and_2_out;

  and and_1 (and_1_out, ~d_i, we_i);  // AND_Gate
  and and_2 (and_2_out, we_i, d_i);
  sr_latch sr_latch_1 (.r_i(and_1_out), .s_i(and_2_out), .q_o(q_o), .q_no(q_no));

  // Notes on the sheet:
  //   Copyright (c) 2026 Guiyuan Zhu. All rights reserved.
endmodule

module d_latch_rst_v1 (
  input  rst_i,
  input  we_i,
  input  d_i,
  output q_o,
  output q_no
);

  wire multiplexer_1_out, multiplexer_2_out;

  Multiplexer multiplexer_1 (.in0(we_i), .in1(1'b1), .out(multiplexer_1_out), .sel(rst_i));
  Multiplexer multiplexer_2 (.in0(d_i), .in1(1'b0), .out(multiplexer_2_out), .sel(rst_i));
  d_latch d_latch_1 (.we_i(multiplexer_1_out), .d_i(multiplexer_2_out), .q_o(q_o), .q_no(q_no));

  // Notes on the sheet:
  //   Copyright (c) 2026 Guiyuan Zhu. All rights reserved.
endmodule

module d_latch_rst_v2 (
  input  rst_i,
  input  we_i,
  input  d_i,
  output q_o,
  output q_no
);

  wire and_1_out, and_2_out, or_1_out;

  or or_1 (or_1_out, rst_i, and_1_out);
  and and_1 (and_1_out, ~d_i, we_i);  // AND_Gate
  and and_2 (and_2_out, we_i, ~rst_i, d_i);  // AND_Gate
  sr_latch sr_latch_1 (.r_i(or_1_out), .s_i(and_2_out), .q_o(q_o), .q_no(q_no));

  // Notes on the sheet:
  //   Copyright (c) 2026 Guiyuan Zhu. All rights reserved.
endmodule

module d_latch_rst_flip_top (
);

  wire button_1_out, button_2_out, d_latch_rst_v1_1_q_o, not_1_out;

  Button button_1 (.out(button_1_out));
  not not_1 (not_1_out, d_latch_rst_v1_1_q_o);
  Button button_2 (.out(button_2_out));
  d_latch_rst_v1 d_latch_rst_v1_1 (
    .rst_i(button_2_out), .we_i(not_1_out), .d_i(button_1_out), .q_o(d_latch_rst_v1_1_q_o));  // open: q_no

  // Notes on the sheet:
  //   Copyright (c) 2026 Guiyuan Zhu. All rights reserved.
endmodule

module d_flip_flop_v1 (
  input  clk_i,
  input  d_i,
  output q_o,
  output q_no
);

  wire d_latch_1_q_o, not_1_out;

  not not_1 (not_1_out, clk_i);
  d_latch d_latch_1 (.we_i(not_1_out), .d_i(d_i), .q_o(d_latch_1_q_o));  // open: q_no
  d_latch d_latch_2 (.we_i(clk_i), .d_i(d_latch_1_q_o), .q_o(q_o), .q_no(q_no));

  // Notes on the sheet:
  //   Copyright (c) 2026 Guiyuan Zhu. All rights reserved.
endmodule

module d_flip_flop_top (
  input  in_1
);

  wire button_1_out, d_flip_flop_v1_1_q_o;

  Button button_1 (.out(button_1_out));
  LED led_1 (.in(d_flip_flop_v1_1_q_o));
  d_flip_flop_v1 d_flip_flop_v1_1 (.clk_i(button_1_out), .d_i(in_1), .q_o(d_flip_flop_v1_1_q_o));  // open: q_no

  // Notes on the sheet:
  //   Copyright (c) 2026 Guiyuan Zhu. All rights reserved.
endmodule

module d_flip_flop_rst (
  input  rst_i,
  input  clk_i,
  input  d_i,
  output q_o
);

  wire d_latch_1_q_o, not_1_out;

  not not_1 (not_1_out, clk_i);
  d_latch d_latch_1 (.we_i(not_1_out), .d_i(d_i), .q_o(d_latch_1_q_o));  // open: q_no
  d_latch_rst_v2 d_latch_rst_v2_1 (.rst_i(rst_i), .we_i(clk_i), .d_i(d_latch_1_q_o), .q_o(q_o));  // open: q_no

  // Notes on the sheet:
  //   Copyright (c) 2026 Guiyuan Zhu. All rights reserved.
endmodule

module d_flip_flop_rst_top (
);

  wire button_1_out, button_2_out, d_flip_flop_rst_1_q_o, not_1_out;

  Button button_1 (.out(button_1_out));
  Button button_2 (.out(button_2_out));
  not not_1 (not_1_out, d_flip_flop_rst_1_q_o);
  d_flip_flop_rst d_flip_flop_rst_1 (
    .rst_i(button_1_out), .clk_i(button_2_out), .d_i(not_1_out), .q_o(d_flip_flop_rst_1_q_o));

  // Notes on the sheet:
  //   Copyright (c) 2026 Guiyuan Zhu. All rights reserved.
endmodule

module d_flip_flop_neg (
  input  clk_i,
  input  d_i,
  output q_o
);

  wire d_latch_1_q_o, not_1_out;

  not not_1 (not_1_out, clk_i);
  d_latch d_latch_1 (.we_i(clk_i), .d_i(d_i), .q_o(d_latch_1_q_o));  // open: q_no
  d_latch d_latch_2 (.we_i(not_1_out), .d_i(d_latch_1_q_o), .q_o(q_o));  // open: q_no

  // Notes on the sheet:
  //   Copyright (c) 2026 Guiyuan Zhu. All rights reserved.
endmodule

module d_flip_flop_v2 (
  input  clk_i,
  input  d_i,
  output q_o,
  output q_no
);

  wire nand_1_out, nand_2_out, nand_3_out, nand_4_out;

  nand nand_1 (nand_1_out, nand_4_out, nand_2_out);
  nand nand_2 (nand_2_out, nand_1_out, clk_i);
  nand nand_3 (nand_3_out, nand_2_out, clk_i, nand_4_out);
  nand nand_4 (nand_4_out, nand_3_out, d_i);
  nand nand_5 (q_o, nand_2_out, q_no);
  nand nand_6 (q_no, q_o, nand_3_out);

  // Notes on the sheet:
  //   Copyright (c) 2026 Guiyuan Zhu. All rights reserved.
endmodule

module d_flip_flop_en_v1 (
  input  d_i,
  input  en_i,
  input  clk_i,
  output q_o,
  output q_no
);

  wire multiplexer_1_out;

  Multiplexer multiplexer_1 (.in0(q_o), .in1(d_i), .out(multiplexer_1_out), .sel(en_i));
  d_flip_flop_v1 d_flip_flop_v1_1 (.clk_i(clk_i), .d_i(multiplexer_1_out), .q_o(q_o), .q_no(q_no));

  // Notes on the sheet:
  //   Copyright (c) 2026 Guiyuan Zhu. All rights reserved.
endmodule

module d_flip_flop_en_v2 (
  input  d_i,
  input  en_i,
  input  clk_i,
  output q_o,
  output q_no
);

  wire and_1_out;

  and and_1 (and_1_out, en_i, clk_i);
  d_flip_flop_v1 d_flip_flop_v1_1 (.clk_i(and_1_out), .d_i(d_i), .q_o(q_o), .q_no(q_no));

  // Notes on the sheet:
  //   Copyright (c) 2026 Guiyuan Zhu. All rights reserved.
endmodule

module reg_4b_rst (
  input  [3:0] d_i,
  input  rst_i,
  input  clk_i,
  output [3:0] q_o
);

  d_flip_flop_rst d_flip_flop_rst_1 (.rst_i(rst_i), .clk_i(clk_i), .d_i(d_i[0]), .q_o(q_o[0]));
  d_flip_flop_rst d_flip_flop_rst_2 (.rst_i(rst_i), .clk_i(clk_i), .d_i(d_i[1]), .q_o(q_o[1]));
  d_flip_flop_rst d_flip_flop_rst_3 (.rst_i(rst_i), .clk_i(clk_i), .d_i(d_i[2]), .q_o(q_o[2]));
  d_flip_flop_rst d_flip_flop_rst_4 (.rst_i(rst_i), .clk_i(clk_i), .d_i(d_i[3]), .q_o(q_o[3]));

  // Notes on the sheet:
  //   Copyright (c) 2026 Guiyuan Zhu. All rights reserved.
endmodule

module reg_4b_rst_top (
);

  wire button_1_out, dipswitch_1_sw5;
  wire [3:0] dipswitch_1_sw4, reg_4b_rst_1_q_o;

  DipSwitch #(.number(5)) dipswitch_1 (
    .sw1(dipswitch_1_sw4[3]), .sw2(dipswitch_1_sw4[2]), .sw3(dipswitch_1_sw4[1]), .sw4(dipswitch_1_sw4[0]),
    .sw5(dipswitch_1_sw5));
  Button button_1 (.out(button_1_out));
  reg_4b_rst reg_4b_rst_1 (
    .d_i(dipswitch_1_sw4), .rst_i(dipswitch_1_sw5), .clk_i(button_1_out), .q_o(reg_4b_rst_1_q_o));
  segment_mux segment_mux_1 (.data_i(reg_4b_rst_1_q_o));  // open: dec_i

  // Notes on the sheet:
  //   Copyright (c) 2026 Guiyuan Zhu. All rights reserved.
endmodule

module half_subber_1b (
  input  a_i,
  input  b_i,
  output sub_o,
  output borrow_o
);

  xor xor_1 (sub_o, a_i, b_i);
  and and_1 (borrow_o, ~a_i, b_i);  // AND_Gate

  // Notes on the sheet:
  //   Copyright (c) 2026 Guiyuan Zhu. All rights reserved.
endmodule

module full_subber_1b_v1 (
  input  bin_i,
  input  a_i,
  input  b_i,
  output diff_o,
  output bout_o
);

  wire and_1_out, and_2_out, xor_1_out;

  xor xor_1 (xor_1_out, a_i, b_i);
  and and_1 (and_1_out, ~a_i, b_i);  // AND_Gate
  xor xor_2 (diff_o, xor_1_out, bin_i);
  and and_2 (and_2_out, ~xor_1_out, bin_i);  // AND_Gate
  or or_1 (bout_o, and_2_out, and_1_out);

  // Notes on the sheet:
  //   Copyright (c) 2026 Guiyuan Zhu. All rights reserved.
endmodule

module full_subber_1b_v2 (
  input  bin_i,
  input  a_i,
  input  b_i,
  output diff_o,
  output bout_o
);

  wire half_subber_1b_1_borrow_o, half_subber_1b_2_borrow_o, half_subber_1b_2_sub_o;

  half_subber_1b half_subber_1b_1 (
    .a_i(half_subber_1b_2_sub_o), .b_i(bin_i), .sub_o(diff_o), .borrow_o(half_subber_1b_1_borrow_o));
  half_subber_1b half_subber_1b_2 (
    .a_i(a_i), .b_i(b_i), .sub_o(half_subber_1b_2_sub_o), .borrow_o(half_subber_1b_2_borrow_o));
  or or_1 (bout_o, half_subber_1b_1_borrow_o, half_subber_1b_2_borrow_o);

  // Notes on the sheet:
  //   Copyright (c) 2026 Guiyuan Zhu. All rights reserved.
endmodule

module rcs_4b (
  input  bin_i,
  input  [3:0] a_i,
  input  [3:0] b_i,
  output [3:0] diff_o,
  output bout_o
);

  wire full_subber_1b_v2_1_bout_o, full_subber_1b_v2_2_bout_o, full_subber_1b_v2_3_bout_o;

  full_subber_1b_v2 full_subber_1b_v2_1 (
    .bin_i(bin_i), .a_i(a_i[0]), .b_i(b_i[0]), .diff_o(diff_o[0]), .bout_o(full_subber_1b_v2_1_bout_o));
  full_subber_1b_v2 full_subber_1b_v2_2 (
    .bin_i(full_subber_1b_v2_1_bout_o), .a_i(a_i[1]), .b_i(b_i[1]), .diff_o(diff_o[1]),
    .bout_o(full_subber_1b_v2_2_bout_o));
  full_subber_1b_v2 full_subber_1b_v2_3 (
    .bin_i(full_subber_1b_v2_2_bout_o), .a_i(a_i[2]), .b_i(b_i[2]), .diff_o(diff_o[2]),
    .bout_o(full_subber_1b_v2_3_bout_o));
  full_subber_1b_v2 full_subber_1b_v2_4 (
    .bin_i(full_subber_1b_v2_3_bout_o), .a_i(a_i[3]), .b_i(b_i[3]), .diff_o(diff_o[3]), .bout_o(bout_o));

  // Notes on the sheet:
  //   Copyright (c) 2026 Guiyuan Zhu. All rights reserved.
endmodule

module suber_top (
  input  [3:0] a_i,
  input  [3:0] b_i
);

  wire bout;
  wire [3:0] diff;

  segment_mux segment_mux_1 (.data_i(a_i));  // open: dec_i
  segment_mux segment_mux_2 (.data_i(diff));  // open: dec_i
  segment_mux segment_mux_3 (.data_i(b_i));  // open: dec_i
  LED led_1 (.in(bout));
  rcs_4b rcs_4b_1 (.bin_i(1'b0), .a_i(a_i), .b_i(b_i), .diff_o(diff), .bout_o(bout));

  // Other names for the same wires on the sheet: a[3:0] = a_i; b[3:0] = b_i

  // Notes on the sheet:
  //   Copyright (c) 2026 Guiyuan Zhu. All rights reserved.
endmodule

module sign_and_magnitude_adder_v1 (
  input  [3:0] a_i,
  input  [3:0] b_i,
  output [3:0] result_o,
  output bout_o,
  output cout_o
);

  wire rcs_4b_1_bout_o, sel_add;
  wire [3:0] rca_4b_raw_1_sum_o, rcs_4b_1_diff_o;

  xnor xnor_1 (sel_add, a_i[3], b_i[3]);
  rca_4b_raw rca_4b_raw_1 (
    .cin_i(1'b0), .a_i({1'b0, a_i[2:0]}), .b_i({1'b0, b_i[2:0]}), .sum_o(rca_4b_raw_1_sum_o));  // open: cout_o
  rcs_4b rcs_4b_1 (
    .bin_i(1'b0), .a_i({1'b0, a_i[2:0]}), .b_i({1'b0, b_i[2:0]}), .diff_o(rcs_4b_1_diff_o),
    .bout_o(rcs_4b_1_bout_o));
  // Probe on rca_4b_raw_1_sum_o[2:0]
  // Probe on rcs_4b_1_diff_o[2:0]
  Multiplexer #(.width(3)) multiplexer_1 (
    .in0(rcs_4b_1_diff_o[2:0]), .in1(rca_4b_raw_1_sum_o[2:0]), .out(result_o[2:0]), .sel(sel_add));
  Multiplexer multiplexer_2 (.in0(a_i[3]), .in1(b_i[3]), .out(result_o[3]), .sel(rcs_4b_1_diff_o[3]));
  and and_1 (bout_o, rcs_4b_1_bout_o, ~sel_add);  // AND_Gate
  and and_2 (cout_o, rca_4b_raw_1_sum_o[3], sel_add);

  // Other names for the same wires on the sheet: sa = a_i[3]; sb = b_i[3]

  // Notes on the sheet:
  //   Copyright (c) 2026 Guiyuan Zhu. All rights reserved.
endmodule

module sign_and_magnitude_adder_top_v1 (
  input  [3:0] a_i,
  input  [3:0] b_i
);

  wire bout, cout, segment_3_7_v2_1_a_o, segment_3_7_v2_1_b_o, segment_3_7_v2_1_c_o, segment_3_7_v2_1_d_o,
       segment_3_7_v2_1_e_o, segment_3_7_v2_1_f_o, segment_3_7_v2_1_g_o, segment_3_7_v2_1_h_o,
       segment_3_7_v2_2_a_o, segment_3_7_v2_2_b_o, segment_3_7_v2_2_c_o, segment_3_7_v2_2_d_o,
       segment_3_7_v2_2_e_o, segment_3_7_v2_2_f_o, segment_3_7_v2_2_g_o, segment_3_7_v2_2_h_o,
       segment_3_7_v2_3_a_o, segment_3_7_v2_3_b_o, segment_3_7_v2_3_c_o, segment_3_7_v2_3_d_o,
       segment_3_7_v2_3_e_o, segment_3_7_v2_3_f_o, segment_3_7_v2_3_g_o, segment_3_7_v2_3_h_o;
  wire [3:0] r;

  segment_3_7_v2 segment_3_7_v2_1 (
    .data_i({1'b0, a_i[2:0]}), .a_o(segment_3_7_v2_1_a_o), .b_o(segment_3_7_v2_1_b_o),
    .c_o(segment_3_7_v2_1_c_o), .d_o(segment_3_7_v2_1_d_o), .e_o(segment_3_7_v2_1_e_o),
    .f_o(segment_3_7_v2_1_f_o), .g_o(segment_3_7_v2_1_g_o), .h_o(segment_3_7_v2_1_h_o));
  segment_3_7_v2 segment_3_7_v2_2 (
    .data_i({1'b0, r[2:0]}), .a_o(segment_3_7_v2_2_a_o), .b_o(segment_3_7_v2_2_b_o),
    .c_o(segment_3_7_v2_2_c_o), .d_o(segment_3_7_v2_2_d_o), .e_o(segment_3_7_v2_2_e_o),
    .f_o(segment_3_7_v2_2_f_o), .g_o(segment_3_7_v2_2_g_o), .h_o(segment_3_7_v2_2_h_o));
  _7_Segment_Display u_7_segment_display_1 (.g(r[3]));  // open: f, a, b, e, d, c, dp
  _7_Segment_Display u_7_segment_display_2 (.g(a_i[3]));  // open: f, a, b, e, d, c, dp
  _7_Segment_Display u_7_segment_display_3 (
    .g(segment_3_7_v2_1_g_o), .f(segment_3_7_v2_1_f_o), .a(segment_3_7_v2_1_a_o), .b(segment_3_7_v2_1_b_o),
    .e(segment_3_7_v2_1_e_o), .d(segment_3_7_v2_1_d_o), .c(segment_3_7_v2_1_c_o), .dp(segment_3_7_v2_1_h_o));
  _7_Segment_Display u_7_segment_display_4 (
    .g(segment_3_7_v2_2_g_o), .f(segment_3_7_v2_2_f_o), .a(segment_3_7_v2_2_a_o), .b(segment_3_7_v2_2_b_o),
    .e(segment_3_7_v2_2_e_o), .d(segment_3_7_v2_2_d_o), .c(segment_3_7_v2_2_c_o), .dp(segment_3_7_v2_2_h_o));
  sign_and_magnitude_adder_v1 sign_and_magnitude_adder_v1_1 (
    .a_i(a_i), .b_i(b_i), .result_o(r), .bout_o(bout), .cout_o(cout));
  LED led_1 (.in(cout));
  LED led_2 (.in(bout));
  segment_3_7_v2 segment_3_7_v2_3 (
    .data_i({1'b0, b_i[2:0]}), .a_o(segment_3_7_v2_3_a_o), .b_o(segment_3_7_v2_3_b_o),
    .c_o(segment_3_7_v2_3_c_o), .d_o(segment_3_7_v2_3_d_o), .e_o(segment_3_7_v2_3_e_o),
    .f_o(segment_3_7_v2_3_f_o), .g_o(segment_3_7_v2_3_g_o), .h_o(segment_3_7_v2_3_h_o));
  _7_Segment_Display u_7_segment_display_5 (.g(b_i[3]));  // open: f, a, b, e, d, c, dp
  _7_Segment_Display u_7_segment_display_6 (
    .g(segment_3_7_v2_3_g_o), .f(segment_3_7_v2_3_f_o), .a(segment_3_7_v2_3_a_o), .b(segment_3_7_v2_3_b_o),
    .e(segment_3_7_v2_3_e_o), .d(segment_3_7_v2_3_d_o), .c(segment_3_7_v2_3_c_o), .dp(segment_3_7_v2_3_h_o));

  // Other names for the same wires on the sheet: a[3:0] = a_i; va[2:0] = a_i[2:0]; sa = a_i[3]; b[3:0] = b_i;
  //   vb[2:0] = b_i[2:0]; sb = b_i[3]; vr[2:0] = r[2:0]; sr = r[3]

  // Notes on the sheet:
  //   Copyright (c) 2026 Guiyuan Zhu. All rights reserved.
endmodule

module sign_and_magnitude_adder_v2 (
  input  [3:0] a_i,
  input  [3:0] b_i,
  output [4:0] result_o
);

  wire rcs_4b_1_bout_o, sel_add;
  wire [2:0] multiplexer_1_out;
  wire [3:0] rca_4b_raw_1_sum_o, rcs_4b_1_diff_o, rcs_4b_2_diff_o;

  xnor xnor_1 (sel_add, a_i[3], b_i[3]);
  rca_4b_raw rca_4b_raw_1 (
    .cin_i(1'b0), .a_i({1'b0, a_i[2:0]}), .b_i({1'b0, b_i[2:0]}), .sum_o(rca_4b_raw_1_sum_o));  // open: cout_o
  rcs_4b rcs_4b_1 (
    .bin_i(1'b0), .a_i({1'b0, a_i[2:0]}), .b_i({1'b0, b_i[2:0]}), .diff_o(rcs_4b_1_diff_o),
    .bout_o(rcs_4b_1_bout_o));
  rcs_4b rcs_4b_2 (
    .bin_i(1'b0), .a_i({1'b0, b_i[2:0]}), .b_i({1'b0, a_i[2:0]}), .diff_o(rcs_4b_2_diff_o));  // open: bout_o
  Multiplexer #(.width(3)) multiplexer_1 (
    .in0(rcs_4b_1_diff_o[2:0]), .in1(rcs_4b_2_diff_o[2:0]), .out(multiplexer_1_out), .sel(rcs_4b_1_bout_o));
  // Probe on rca_4b_raw_1_sum_o
  // Probe on {1'b0, multiplexer_1_out}
  Multiplexer #(.width(4)) multiplexer_2 (
    .in0({1'b0, multiplexer_1_out}), .in1(rca_4b_raw_1_sum_o), .out(result_o[3:0]), .sel(sel_add));
  Multiplexer multiplexer_3 (.in0(a_i[3]), .in1(b_i[3]), .out(result_o[4]), .sel(rcs_4b_1_diff_o[3]));

  // Other names for the same wires on the sheet: sa = a_i[3]; sb = b_i[3]

  // Notes on the sheet:
  //   Copyright (c) 2026 Guiyuan Zhu. All rights reserved.
endmodule

module sign_and_magnitude_adder_top_v2 (
  input  [3:0] a_i,
  input  [3:0] b_i
);

  wire segment_3_7_v2_1_a_o, segment_3_7_v2_1_b_o, segment_3_7_v2_1_c_o, segment_3_7_v2_1_d_o,
       segment_3_7_v2_1_e_o, segment_3_7_v2_1_f_o, segment_3_7_v2_1_g_o, segment_3_7_v2_1_h_o,
       segment_3_7_v2_2_a_o, segment_3_7_v2_2_b_o, segment_3_7_v2_2_c_o, segment_3_7_v2_2_d_o,
       segment_3_7_v2_2_e_o, segment_3_7_v2_2_f_o, segment_3_7_v2_2_g_o, segment_3_7_v2_2_h_o,
       segment_3_7_v2_3_a_o, segment_3_7_v2_3_b_o, segment_3_7_v2_3_c_o, segment_3_7_v2_3_d_o,
       segment_3_7_v2_3_e_o, segment_3_7_v2_3_f_o, segment_3_7_v2_3_g_o, segment_3_7_v2_3_h_o;
  wire [4:0] r;

  segment_3_7_v2 segment_3_7_v2_1 (
    .data_i({1'b0, a_i[2:0]}), .a_o(segment_3_7_v2_1_a_o), .b_o(segment_3_7_v2_1_b_o),
    .c_o(segment_3_7_v2_1_c_o), .d_o(segment_3_7_v2_1_d_o), .e_o(segment_3_7_v2_1_e_o),
    .f_o(segment_3_7_v2_1_f_o), .g_o(segment_3_7_v2_1_g_o), .h_o(segment_3_7_v2_1_h_o));
  segment_3_7_v2 segment_3_7_v2_2 (
    .data_i(r[3:0]), .a_o(segment_3_7_v2_2_a_o), .b_o(segment_3_7_v2_2_b_o), .c_o(segment_3_7_v2_2_c_o),
    .d_o(segment_3_7_v2_2_d_o), .e_o(segment_3_7_v2_2_e_o), .f_o(segment_3_7_v2_2_f_o),
    .g_o(segment_3_7_v2_2_g_o), .h_o(segment_3_7_v2_2_h_o));
  _7_Segment_Display u_7_segment_display_1 (.g(r[4]));  // open: f, a, b, e, d, c, dp
  _7_Segment_Display u_7_segment_display_2 (.g(a_i[3]));  // open: f, a, b, e, d, c, dp
  _7_Segment_Display u_7_segment_display_3 (
    .g(segment_3_7_v2_1_g_o), .f(segment_3_7_v2_1_f_o), .a(segment_3_7_v2_1_a_o), .b(segment_3_7_v2_1_b_o),
    .e(segment_3_7_v2_1_e_o), .d(segment_3_7_v2_1_d_o), .c(segment_3_7_v2_1_c_o), .dp(segment_3_7_v2_1_h_o));
  _7_Segment_Display u_7_segment_display_4 (
    .g(segment_3_7_v2_2_g_o), .f(segment_3_7_v2_2_f_o), .a(segment_3_7_v2_2_a_o), .b(segment_3_7_v2_2_b_o),
    .e(segment_3_7_v2_2_e_o), .d(segment_3_7_v2_2_d_o), .c(segment_3_7_v2_2_c_o), .dp(segment_3_7_v2_2_h_o));
  sign_and_magnitude_adder_v2 sign_and_magnitude_adder_v2_1 (.a_i(a_i), .b_i(b_i), .result_o(r));
  segment_3_7_v2 segment_3_7_v2_3 (
    .data_i({1'b0, b_i[2:0]}), .a_o(segment_3_7_v2_3_a_o), .b_o(segment_3_7_v2_3_b_o),
    .c_o(segment_3_7_v2_3_c_o), .d_o(segment_3_7_v2_3_d_o), .e_o(segment_3_7_v2_3_e_o),
    .f_o(segment_3_7_v2_3_f_o), .g_o(segment_3_7_v2_3_g_o), .h_o(segment_3_7_v2_3_h_o));
  _7_Segment_Display u_7_segment_display_5 (.g(b_i[3]));  // open: f, a, b, e, d, c, dp
  _7_Segment_Display u_7_segment_display_6 (
    .g(segment_3_7_v2_3_g_o), .f(segment_3_7_v2_3_f_o), .a(segment_3_7_v2_3_a_o), .b(segment_3_7_v2_3_b_o),
    .e(segment_3_7_v2_3_e_o), .d(segment_3_7_v2_3_d_o), .c(segment_3_7_v2_3_c_o), .dp(segment_3_7_v2_3_h_o));

  // Other names for the same wires on the sheet: a[3:0] = a_i; va[2:0] = a_i[2:0]; sa = a_i[3]; b[3:0] = b_i;
  //   vb[2:0] = b_i[2:0]; sb = b_i[3]; vr[3:0] = r[3:0]; sr = r[4]

  // Notes on the sheet:
  //   Copyright (c) 2026 Guiyuan Zhu. All rights reserved.
endmodule

module ones_complement_adder_v1 (
  input  [3:0] a_i,
  input  [3:0] b_i,
  output [3:0] result_o,
  output oveflow_o
);

  wire [2:0] bit_extender_1_out, bit_extender_2_out, bit_extender_3_out,
       sign_and_magnitude_adder_v2_1_result_o, xor_1_out, xor_2_out;

  assign bit_extender_1_out = {{2{a_i[3]}}, a_i[3]};  // Bit_Extender bit_extender_1
  assign bit_extender_2_out = {{2{b_i[3]}}, b_i[3]};  // Bit_Extender bit_extender_2
  assign xor_1_out = bit_extender_1_out ^ a_i[2:0];  // XOR_Gate xor_1, 3 bits wide
  assign xor_2_out = bit_extender_2_out ^ b_i[2:0];  // XOR_Gate xor_2, 3 bits wide
  sign_and_magnitude_adder_v2 sign_and_magnitude_adder_v2_1 (
    .a_i({a_i[3], xor_1_out}), .b_i({b_i[3], xor_2_out}),
    .result_o({result_o[3], oveflow_o, sign_and_magnitude_adder_v2_1_result_o}));
  assign bit_extender_3_out = {{2{result_o[3]}}, result_o[3]};  // Bit_Extender bit_extender_3
  assign result_o[2:0] = sign_and_magnitude_adder_v2_1_result_o ^ bit_extender_3_out;  // XOR_Gate xor_3, 3 bits wide

  // Notes on the sheet:
  //   Copyright (c) 2026 Guiyuan Zhu. All rights reserved.
endmodule

module ones_complement_adder_top_v1 (
  input  [3:0] a_i,
  input  [3:0] b_i
);

  wire ovf, segment_3_7_v2_1_a_o, segment_3_7_v2_1_b_o, segment_3_7_v2_1_c_o, segment_3_7_v2_1_d_o,
       segment_3_7_v2_1_e_o, segment_3_7_v2_1_f_o, segment_3_7_v2_1_g_o, segment_3_7_v2_1_h_o,
       segment_3_7_v2_2_a_o, segment_3_7_v2_2_b_o, segment_3_7_v2_2_c_o, segment_3_7_v2_2_d_o,
       segment_3_7_v2_2_e_o, segment_3_7_v2_2_f_o, segment_3_7_v2_2_g_o, segment_3_7_v2_2_h_o,
       segment_3_7_v2_3_a_o, segment_3_7_v2_3_b_o, segment_3_7_v2_3_c_o, segment_3_7_v2_3_d_o,
       segment_3_7_v2_3_e_o, segment_3_7_v2_3_f_o, segment_3_7_v2_3_g_o, segment_3_7_v2_3_h_o;
  wire [2:0] bit_extender_1_out, bit_extender_2_out, bit_extender_3_out, va, vb, vr;
  wire [3:0] r;

  assign bit_extender_1_out = {{2{a_i[3]}}, a_i[3]};  // Bit_Extender bit_extender_1
  assign bit_extender_2_out = {{2{b_i[3]}}, b_i[3]};  // Bit_Extender bit_extender_2
  assign bit_extender_3_out = {{2{r[3]}}, r[3]};  // Bit_Extender bit_extender_3
  assign va = bit_extender_1_out ^ a_i[2:0];  // XOR_Gate xor_1, 3 bits wide
  assign vb = bit_extender_2_out ^ b_i[2:0];  // XOR_Gate xor_2, 3 bits wide
  assign vr = bit_extender_3_out ^ r[2:0];  // XOR_Gate xor_3, 3 bits wide
  segment_3_7_v2 segment_3_7_v2_1 (
    .data_i({1'b0, va}), .a_o(segment_3_7_v2_1_a_o), .b_o(segment_3_7_v2_1_b_o), .c_o(segment_3_7_v2_1_c_o),
    .d_o(segment_3_7_v2_1_d_o), .e_o(segment_3_7_v2_1_e_o), .f_o(segment_3_7_v2_1_f_o),
    .g_o(segment_3_7_v2_1_g_o), .h_o(segment_3_7_v2_1_h_o));
  segment_3_7_v2 segment_3_7_v2_2 (
    .data_i({1'b0, vr}), .a_o(segment_3_7_v2_2_a_o), .b_o(segment_3_7_v2_2_b_o), .c_o(segment_3_7_v2_2_c_o),
    .d_o(segment_3_7_v2_2_d_o), .e_o(segment_3_7_v2_2_e_o), .f_o(segment_3_7_v2_2_f_o),
    .g_o(segment_3_7_v2_2_g_o), .h_o(segment_3_7_v2_2_h_o));
  ones_complement_adder_v1 ones_complement_adder_v1_1 (.a_i(a_i), .b_i(b_i), .result_o(r), .oveflow_o(ovf));
  _7_Segment_Display u_7_segment_display_1 (.g(a_i[3]));  // open: f, a, b, e, d, c, dp
  _7_Segment_Display u_7_segment_display_2 (
    .g(segment_3_7_v2_1_g_o), .f(segment_3_7_v2_1_f_o), .a(segment_3_7_v2_1_a_o), .b(segment_3_7_v2_1_b_o),
    .e(segment_3_7_v2_1_e_o), .d(segment_3_7_v2_1_d_o), .c(segment_3_7_v2_1_c_o), .dp(segment_3_7_v2_1_h_o));
  _7_Segment_Display u_7_segment_display_3 (.g(r[3]));  // open: f, a, b, e, d, c, dp
  _7_Segment_Display u_7_segment_display_4 (
    .g(segment_3_7_v2_2_g_o), .f(segment_3_7_v2_2_f_o), .a(segment_3_7_v2_2_a_o), .b(segment_3_7_v2_2_b_o),
    .e(segment_3_7_v2_2_e_o), .d(segment_3_7_v2_2_d_o), .c(segment_3_7_v2_2_c_o), .dp(segment_3_7_v2_2_h_o));
  LED led_1 (.in(ovf));
  segment_3_7_v2 segment_3_7_v2_3 (
    .data_i({1'b0, vb}), .a_o(segment_3_7_v2_3_a_o), .b_o(segment_3_7_v2_3_b_o), .c_o(segment_3_7_v2_3_c_o),
    .d_o(segment_3_7_v2_3_d_o), .e_o(segment_3_7_v2_3_e_o), .f_o(segment_3_7_v2_3_f_o),
    .g_o(segment_3_7_v2_3_g_o), .h_o(segment_3_7_v2_3_h_o));
  _7_Segment_Display u_7_segment_display_5 (.g(b_i[3]));  // open: f, a, b, e, d, c, dp
  _7_Segment_Display u_7_segment_display_6 (
    .g(segment_3_7_v2_3_g_o), .f(segment_3_7_v2_3_f_o), .a(segment_3_7_v2_3_a_o), .b(segment_3_7_v2_3_b_o),
    .e(segment_3_7_v2_3_e_o), .d(segment_3_7_v2_3_d_o), .c(segment_3_7_v2_3_c_o), .dp(segment_3_7_v2_3_h_o));

  // Other names for the same wires on the sheet: a[3:0] = a_i; sa = a_i[3]; b[3:0] = b_i; sb = b_i[3]; sr = r[3]

  // Notes on the sheet:
  //   Copyright (c) 2026 Guiyuan Zhu. All rights reserved.
endmodule

module ones_complement_adder_v2 (
  input  [3:0] a_i,
  input  [3:0] b_i,
  output [3:0] result_o,
  output overflow_o
);

  wire rca_4b_raw_1_cout_o, xor_1_out, xor_2_out;
  wire [3:0] rca_4b_raw_1_sum_o;

  rca_4b_raw rca_4b_raw_1 (
    .cin_i(1'b0), .a_i(a_i), .b_i(b_i), .sum_o(rca_4b_raw_1_sum_o), .cout_o(rca_4b_raw_1_cout_o));
  rca_4b_raw rca_4b_raw_2 (
    .cin_i(rca_4b_raw_1_cout_o), .a_i(rca_4b_raw_1_sum_o), .b_i(4'b0000), .sum_o(result_o));  // open: cout_o
  xor xor_1 (xor_1_out, a_i[3], b_i[3]);
  xor xor_2 (xor_2_out, b_i[3], result_o[3]);
  and and_1 (overflow_o, ~xor_1_out, xor_2_out);  // AND_Gate

  // Other names for the same wires on the sheet: a[3:0] = a_i; b[3:0] = b_i; r[3:0] = result_o

  // Notes on the sheet:
  //   Copyright (c) 2026 Guiyuan Zhu. All rights reserved.
endmodule

module ones_complement_adder_top_v2 (
  input  [3:0] a_i,
  input  [3:0] b_i
);

  wire ovf, segment_3_7_v2_1_a_o, segment_3_7_v2_1_b_o, segment_3_7_v2_1_c_o, segment_3_7_v2_1_d_o,
       segment_3_7_v2_1_e_o, segment_3_7_v2_1_f_o, segment_3_7_v2_1_g_o, segment_3_7_v2_1_h_o,
       segment_3_7_v2_2_a_o, segment_3_7_v2_2_b_o, segment_3_7_v2_2_c_o, segment_3_7_v2_2_d_o,
       segment_3_7_v2_2_e_o, segment_3_7_v2_2_f_o, segment_3_7_v2_2_g_o, segment_3_7_v2_2_h_o,
       segment_3_7_v2_3_a_o, segment_3_7_v2_3_b_o, segment_3_7_v2_3_c_o, segment_3_7_v2_3_d_o,
       segment_3_7_v2_3_e_o, segment_3_7_v2_3_f_o, segment_3_7_v2_3_g_o, segment_3_7_v2_3_h_o;
  wire [2:0] bit_extender_1_out, bit_extender_2_out, bit_extender_3_out, va, vb, vr;
  wire [3:0] r;

  assign bit_extender_1_out = {{2{a_i[3]}}, a_i[3]};  // Bit_Extender bit_extender_1
  assign bit_extender_2_out = {{2{b_i[3]}}, b_i[3]};  // Bit_Extender bit_extender_2
  assign bit_extender_3_out = {{2{r[3]}}, r[3]};  // Bit_Extender bit_extender_3
  assign va = bit_extender_1_out ^ a_i[2:0];  // XOR_Gate xor_1, 3 bits wide
  assign vb = bit_extender_2_out ^ b_i[2:0];  // XOR_Gate xor_2, 3 bits wide
  assign vr = bit_extender_3_out ^ r[2:0];  // XOR_Gate xor_3, 3 bits wide
  segment_3_7_v2 segment_3_7_v2_1 (
    .data_i({1'b0, va}), .a_o(segment_3_7_v2_1_a_o), .b_o(segment_3_7_v2_1_b_o), .c_o(segment_3_7_v2_1_c_o),
    .d_o(segment_3_7_v2_1_d_o), .e_o(segment_3_7_v2_1_e_o), .f_o(segment_3_7_v2_1_f_o),
    .g_o(segment_3_7_v2_1_g_o), .h_o(segment_3_7_v2_1_h_o));
  segment_3_7_v2 segment_3_7_v2_2 (
    .data_i({1'b0, vr}), .a_o(segment_3_7_v2_2_a_o), .b_o(segment_3_7_v2_2_b_o), .c_o(segment_3_7_v2_2_c_o),
    .d_o(segment_3_7_v2_2_d_o), .e_o(segment_3_7_v2_2_e_o), .f_o(segment_3_7_v2_2_f_o),
    .g_o(segment_3_7_v2_2_g_o), .h_o(segment_3_7_v2_2_h_o));
  ones_complement_adder_v2 ones_complement_adder_v2_1 (.a_i(a_i), .b_i(b_i), .result_o(r), .overflow_o(ovf));
  _7_Segment_Display u_7_segment_display_1 (.g(a_i[3]));  // open: f, a, b, e, d, c, dp
  _7_Segment_Display u_7_segment_display_2 (
    .g(segment_3_7_v2_1_g_o), .f(segment_3_7_v2_1_f_o), .a(segment_3_7_v2_1_a_o), .b(segment_3_7_v2_1_b_o),
    .e(segment_3_7_v2_1_e_o), .d(segment_3_7_v2_1_d_o), .c(segment_3_7_v2_1_c_o), .dp(segment_3_7_v2_1_h_o));
  _7_Segment_Display u_7_segment_display_3 (.g(r[3]));  // open: f, a, b, e, d, c, dp
  _7_Segment_Display u_7_segment_display_4 (
    .g(segment_3_7_v2_2_g_o), .f(segment_3_7_v2_2_f_o), .a(segment_3_7_v2_2_a_o), .b(segment_3_7_v2_2_b_o),
    .e(segment_3_7_v2_2_e_o), .d(segment_3_7_v2_2_d_o), .c(segment_3_7_v2_2_c_o), .dp(segment_3_7_v2_2_h_o));
  LED led_1 (.in(ovf));
  segment_3_7_v2 segment_3_7_v2_3 (
    .data_i({1'b0, vb}), .a_o(segment_3_7_v2_3_a_o), .b_o(segment_3_7_v2_3_b_o), .c_o(segment_3_7_v2_3_c_o),
    .d_o(segment_3_7_v2_3_d_o), .e_o(segment_3_7_v2_3_e_o), .f_o(segment_3_7_v2_3_f_o),
    .g_o(segment_3_7_v2_3_g_o), .h_o(segment_3_7_v2_3_h_o));
  _7_Segment_Display u_7_segment_display_5 (.g(b_i[3]));  // open: f, a, b, e, d, c, dp
  _7_Segment_Display u_7_segment_display_6 (
    .g(segment_3_7_v2_3_g_o), .f(segment_3_7_v2_3_f_o), .a(segment_3_7_v2_3_a_o), .b(segment_3_7_v2_3_b_o),
    .e(segment_3_7_v2_3_e_o), .d(segment_3_7_v2_3_d_o), .c(segment_3_7_v2_3_c_o), .dp(segment_3_7_v2_3_h_o));

  // Other names for the same wires on the sheet: a[3:0] = a_i; sa = a_i[3]; b[3:0] = b_i; sb = b_i[3]; sr = r[3]

  // Notes on the sheet:
  //   Copyright (c) 2026 Guiyuan Zhu. All rights reserved.
endmodule

module rca_4b (
  input  cin_i,
  input  [3:0] a_i,
  input  [3:0] b_i,
  output [3:0] sum_o,
  output overflow_o,
  output cout_o
);

  wire full_adder_1b_v2_1_cout_o, full_adder_1b_v2_2_cout_o, full_adder_1b_v2_3_cout_o;

  full_adder_1b_v2 full_adder_1b_v2_1 (
    .cin_i(cin_i), .a_i(a_i[0]), .b_i(b_i[0]), .sum_o(sum_o[0]), .cout_o(full_adder_1b_v2_1_cout_o));
  full_adder_1b_v2 full_adder_1b_v2_2 (
    .cin_i(full_adder_1b_v2_1_cout_o), .a_i(a_i[1]), .b_i(b_i[1]), .sum_o(sum_o[1]),
    .cout_o(full_adder_1b_v2_2_cout_o));
  full_adder_1b_v2 full_adder_1b_v2_3 (
    .cin_i(full_adder_1b_v2_2_cout_o), .a_i(a_i[2]), .b_i(b_i[2]), .sum_o(sum_o[2]),
    .cout_o(full_adder_1b_v2_3_cout_o));
  full_adder_1b_v2 full_adder_1b_v2_4 (
    .cin_i(full_adder_1b_v2_3_cout_o), .a_i(a_i[3]), .b_i(b_i[3]), .sum_o(sum_o[3]), .cout_o(cout_o));
  xor xor_1 (overflow_o, full_adder_1b_v2_3_cout_o, cout_o);

  // Notes on the sheet:
  //   Copyright (c) 2026 Guiyuan Zhu. All rights reserved.
endmodule

module reg_4b (
  input  [3:0] d_i,
  input  en_i,
  input  rst_i,
  input  clk_i,
  output [3:0] q_o
);

  wire [3:0] multiplexer_1_out;

  Multiplexer #(.width(4)) multiplexer_1 (.in0(q_o), .in1(d_i), .out(multiplexer_1_out), .sel(en_i));
  reg_4b_rst reg_4b_rst_1 (.d_i(multiplexer_1_out), .rst_i(rst_i), .clk_i(clk_i), .q_o(q_o));

  // Notes on the sheet:
  //   Copyright (c) 2026 Guiyuan Zhu. All rights reserved.
endmodule

module rca_8b (
  input  cin_i,
  input  [7:0] a_i,
  input  [7:0] b_i,
  output [7:0] sum_o,
  output overflow_o,
  output cout_o
);

  wire rca_4b_1_cout_o;

  rca_4b rca_4b_1 (
    .cin_i(cin_i), .a_i(a_i[3:0]), .b_i(b_i[3:0]), .sum_o(sum_o[3:0]), .cout_o(rca_4b_1_cout_o));  // open: overflow_o
  rca_4b rca_4b_2 (
    .cin_i(rca_4b_1_cout_o), .a_i(a_i[7:4]), .b_i(b_i[7:4]), .sum_o(sum_o[7:4]), .overflow_o(overflow_o),
    .cout_o(cout_o));

  // Notes on the sheet:
  //   Copyright (c) 2026 Guiyuan Zhu. All rights reserved.
endmodule

module reg_8b (
  input  [7:0] d_i,
  input  en_i,
  input  rst_i,
  input  clk_i,
  output [7:0] q_o
);

  wire [3:0] multiplexer_1_out, multiplexer_2_out;

  Multiplexer #(.width(4)) multiplexer_1 (.in0(q_o[3:0]), .in1(d_i[3:0]), .out(multiplexer_1_out), .sel(en_i));
  Multiplexer #(.width(4)) multiplexer_2 (.in0(q_o[7:4]), .in1(d_i[7:4]), .out(multiplexer_2_out), .sel(en_i));
  reg_4b_rst reg_4b_rst_1 (.d_i(multiplexer_1_out), .rst_i(rst_i), .clk_i(clk_i), .q_o(q_o[3:0]));
  reg_4b_rst reg_4b_rst_2 (.d_i(multiplexer_2_out), .rst_i(rst_i), .clk_i(clk_i), .q_o(q_o[7:4]));

  // Notes on the sheet:
  //   Copyright (c) 2026 Guiyuan Zhu. All rights reserved.
endmodule

module adder_4b_top (
);

  wire button_1_out, clock_1_out;
  wire [3:0] rca_4b_1_sum_o, reg_4b_rst_1_q_o;

  Clock clock_1 (.out(clock_1_out));
  rca_4b rca_4b_1 (.a_i(reg_4b_rst_1_q_o), .b_i(4'b0001), .sum_o(rca_4b_1_sum_o));  // open: cin_i, overflow_o, cout_o
  Button button_1 (.out(button_1_out));
  reg_4b_rst reg_4b_rst_1 (.d_i(rca_4b_1_sum_o), .rst_i(button_1_out), .clk_i(clock_1_out), .q_o(reg_4b_rst_1_q_o));
  segment_mux segment_mux_1 (.data_i(reg_4b_rst_1_q_o));  // open: dec_i

  // Notes on the sheet:
  //   Copyright (c) 2026 Guiyuan Zhu. All rights reserved.
endmodule

module sum_1_to_10_top (
);

  wire clk_i, comparator_1_eq, d_flip_flop_rst_1_q_o, multiplexer_1_out, rst_i, running;
  wire [7:0] num, num_next, sum, sum_next;

  Comparator comparator_1 (.a(num), .b(8'ha), .eq(comparator_1_eq));  // open: gt, lt
  Button u_rst_i (.out(rst_i));
  Clock u_clk_i (.out(clk_i));
  Multiplexer multiplexer_1 (.in0(d_flip_flop_rst_1_q_o), .in1(1'b1), .out(multiplexer_1_out), .sel(comparator_1_eq));
  rca_8b rca_8b_1 (.a_i(num), .b_i(8'h1), .sum_o(num_next));  // open: cin_i, overflow_o, cout_o
  // Probe on num
  reg_8b reg_8b_1 (.d_i(num_next), .en_i(running), .rst_i(rst_i), .clk_i(clk_i), .q_o(num));
  not not_1 (running, d_flip_flop_rst_1_q_o);
  d_flip_flop_rst d_flip_flop_rst_1 (
    .rst_i(rst_i), .clk_i(clk_i), .d_i(multiplexer_1_out), .q_o(d_flip_flop_rst_1_q_o));
  segment_mux segment_mux_1 (.data_i(sum[7:4]));  // open: dec_i
  segment_mux segment_mux_2 (.data_i(sum[3:0]));  // open: dec_i
  // Probe on sum_next
  rca_8b rca_8b_2 (.a_i(sum), .b_i(num), .sum_o(sum_next));  // open: cin_i, overflow_o, cout_o
  reg_8b reg_8b_2 (.d_i(sum_next), .en_i(running), .rst_i(rst_i), .clk_i(clk_i), .q_o(sum));

  // Notes on the sheet:
  //   Copyright (c) 2026 Guiyuan Zhu. All rights reserved.
endmodule

module timmer_mm_ss_top (
);

  wire and_1_out, and_2_out, and_3_out, clk_i, comparator_1_eq, comparator_2_eq, comparator_3_eq,
       comparator_4_eq, rst_i;
  wire [3:0] mm_hi, mm_hi_nxt, mm_lo, mm_lo_nxt, rca_4b_1_sum_o, rca_4b_2_sum_o, rca_4b_3_sum_o,
       rca_4b_4_sum_o, ss_hi, ss_hi_nxt, ss_lo, ss_lo_nxt;

  Button u_rst_i (.out(rst_i));
  Clock u_clk_i (.out(clk_i));
  segment_mux segment_mux_1 (.data_i(mm_hi));  // open: dec_i
  Comparator #(.width(4)) comparator_1 (.a(mm_hi), .b(4'b0101), .eq(comparator_1_eq));  // open: gt, lt
  Comparator #(.width(4)) comparator_2 (.a(mm_lo), .b(4'b1001), .eq(comparator_2_eq));  // open: gt, lt
  reg_4b_rst reg_4b_rst_1 (.d_i(mm_hi_nxt), .rst_i(rst_i), .clk_i(clk_i), .q_o(mm_hi));
  reg_4b_rst reg_4b_rst_2 (.d_i(mm_lo_nxt), .rst_i(rst_i), .clk_i(clk_i), .q_o(mm_lo));
  rca_4b rca_4b_1 (.cin_i(and_2_out), .a_i(mm_hi), .sum_o(rca_4b_1_sum_o));  // open: b_i, overflow_o, cout_o
  and and_1 (and_1_out, comparator_1_eq, and_2_out);
  rca_4b rca_4b_2 (.cin_i(and_3_out), .a_i(mm_lo), .sum_o(rca_4b_2_sum_o));  // open: b_i, overflow_o, cout_o
  and and_2 (and_2_out, comparator_2_eq, and_3_out);
  segment_mux segment_mux_2 (.data_i(mm_lo));  // open: dec_i
  Multiplexer #(.width(4)) multiplexer_1 (.in0(rca_4b_1_sum_o), .in1(4'b0000), .out(mm_hi_nxt), .sel(and_1_out));
  Multiplexer #(.width(4)) multiplexer_2 (.in0(rca_4b_2_sum_o), .in1(4'b0000), .out(mm_lo_nxt), .sel(and_2_out));
  segment_mux segment_mux_3 (.data_i(ss_hi));  // open: dec_i
  segment_mux segment_mux_4 (.data_i(ss_lo));  // open: dec_i
  reg_4b_rst reg_4b_rst_3 (.d_i(ss_hi_nxt), .rst_i(rst_i), .clk_i(clk_i), .q_o(ss_hi));
  reg_4b_rst reg_4b_rst_4 (.d_i(ss_lo_nxt), .rst_i(rst_i), .clk_i(clk_i), .q_o(ss_lo));
  rca_4b rca_4b_3 (.cin_i(comparator_4_eq), .a_i(ss_hi), .sum_o(rca_4b_3_sum_o));  // open: b_i, overflow_o, cout_o
  Comparator #(.width(4)) comparator_3 (.a(ss_hi), .b(4'b0101), .eq(comparator_3_eq));  // open: gt, lt
  and and_3 (and_3_out, comparator_3_eq, comparator_4_eq);
  rca_4b rca_4b_4 (.cin_i(1'b1), .a_i(ss_lo), .sum_o(rca_4b_4_sum_o));  // open: b_i, overflow_o, cout_o
  Comparator #(.width(4)) comparator_4 (.a(ss_lo), .b(4'b1001), .eq(comparator_4_eq));  // open: gt, lt
  Multiplexer #(.width(4)) multiplexer_3 (.in0(rca_4b_3_sum_o), .in1(4'b0000), .out(ss_hi_nxt), .sel(and_3_out));
  Multiplexer #(.width(4)) multiplexer_4 (.in0(rca_4b_4_sum_o), .in1(4'b0000), .out(ss_lo_nxt), .sel(comparator_4_eq));

  // Notes on the sheet:
  //   Copyright (c) 2026 Guiyuan Zhu. All rights reserved.
endmodule

module mux4_8b (
  input  [1:0] sel_i,
  input  [7:0] a_i,
  input  [7:0] b_i,
  input  [7:0] c_i,
  input  [7:0] d_i,
  output [7:0] e_o
);

  wire [3:0] decoder_2_4_1_data_o;
  wire [7:0] and_1_out, and_2_out, and_3_out, and_4_out, bit_extender_1_out, bit_extender_2_out,
       bit_extender_3_out, bit_extender_4_out;

  decoder_2_4 decoder_2_4_1 (.data_i(sel_i), .data_o(decoder_2_4_1_data_o));
  assign bit_extender_1_out = {{7{decoder_2_4_1_data_o[0]}}, decoder_2_4_1_data_o[0]};  // Bit_Extender bit_extender_1
  assign bit_extender_2_out = {{7{decoder_2_4_1_data_o[1]}}, decoder_2_4_1_data_o[1]};  // Bit_Extender bit_extender_2
  assign bit_extender_3_out = {{7{decoder_2_4_1_data_o[2]}}, decoder_2_4_1_data_o[2]};  // Bit_Extender bit_extender_3
  assign bit_extender_4_out = {{7{decoder_2_4_1_data_o[3]}}, decoder_2_4_1_data_o[3]};  // Bit_Extender bit_extender_4
  assign and_1_out = bit_extender_1_out & a_i;  // AND_Gate and_1, 8 bits wide
  assign and_2_out = bit_extender_2_out & b_i;  // AND_Gate and_2, 8 bits wide
  assign and_3_out = bit_extender_3_out & c_i;  // AND_Gate and_3, 8 bits wide
  assign and_4_out = bit_extender_4_out & d_i;  // AND_Gate and_4, 8 bits wide
  assign e_o = and_1_out | and_2_out | and_3_out | and_4_out;  // OR_Gate or_1, 8 bits wide

  // Notes on the sheet:
  //   Copyright (c) 2026 Guiyuan Zhu. All rights reserved.
endmodule

module mux8_8b (
  input  [2:0] sel_i,
  input  [7:0] a_i,
  input  [7:0] b_i,
  input  [7:0] c_i,
  input  [7:0] d_i,
  input  [7:0] e_i,
  input  [7:0] f_i,
  input  [7:0] g_i,
  input  [7:0] h_i,
  output [7:0] data_o
);

  wire [7:0] and_1_out, and_2_out, and_3_out, and_4_out, and_5_out, and_6_out, and_7_out, and_8_out,
       bit_extender_1_out, bit_extender_2_out, bit_extender_3_out, bit_extender_4_out, bit_extender_5_out,
       bit_extender_6_out, bit_extender_7_out, bit_extender_8_out, decoder_3_8_1_data_o;

  decoder_3_8 decoder_3_8_1 (.data_i(sel_i), .data_o(decoder_3_8_1_data_o));
  assign bit_extender_1_out = {{7{decoder_3_8_1_data_o[0]}}, decoder_3_8_1_data_o[0]};  // Bit_Extender bit_extender_1
  assign bit_extender_2_out = {{7{decoder_3_8_1_data_o[1]}}, decoder_3_8_1_data_o[1]};  // Bit_Extender bit_extender_2
  assign bit_extender_3_out = {{7{decoder_3_8_1_data_o[2]}}, decoder_3_8_1_data_o[2]};  // Bit_Extender bit_extender_3
  assign bit_extender_4_out = {{7{decoder_3_8_1_data_o[3]}}, decoder_3_8_1_data_o[3]};  // Bit_Extender bit_extender_4
  assign bit_extender_5_out = {{7{decoder_3_8_1_data_o[4]}}, decoder_3_8_1_data_o[4]};  // Bit_Extender bit_extender_5
  assign bit_extender_6_out = {{7{decoder_3_8_1_data_o[5]}}, decoder_3_8_1_data_o[5]};  // Bit_Extender bit_extender_6
  assign bit_extender_7_out = {{7{decoder_3_8_1_data_o[6]}}, decoder_3_8_1_data_o[6]};  // Bit_Extender bit_extender_7
  assign bit_extender_8_out = {{7{decoder_3_8_1_data_o[7]}}, decoder_3_8_1_data_o[7]};  // Bit_Extender bit_extender_8
  assign and_1_out = bit_extender_1_out & a_i;  // AND_Gate and_1, 8 bits wide
  assign and_2_out = bit_extender_2_out & b_i;  // AND_Gate and_2, 8 bits wide
  assign and_3_out = bit_extender_3_out & c_i;  // AND_Gate and_3, 8 bits wide
  assign and_4_out = bit_extender_4_out & d_i;  // AND_Gate and_4, 8 bits wide
  assign and_5_out = bit_extender_5_out & e_i;  // AND_Gate and_5, 8 bits wide
  assign and_6_out = bit_extender_6_out & f_i;  // AND_Gate and_6, 8 bits wide
  assign and_7_out = bit_extender_7_out & g_i;  // AND_Gate and_7, 8 bits wide
  assign and_8_out = bit_extender_8_out & h_i;  // AND_Gate and_8, 8 bits wide
  assign data_o = and_1_out | and_2_out | and_3_out | and_4_out | and_5_out | and_6_out | and_7_out | and_8_out;  // OR_Gate or_1, 8 bits wide

  // Notes on the sheet:
  //   Copyright (c) 2026 Guiyuan Zhu. All rights reserved.
endmodule

module mux16_8b (
  input  [3:0] sel_i,
  input  [7:0] a_i,
  input  [7:0] b_i,
  input  [7:0] c_i,
  input  [7:0] d_i,
  input  [7:0] e_i,
  input  [7:0] f_i,
  input  [7:0] g_i,
  input  [7:0] h_i,
  input  [7:0] i_i,
  input  [7:0] j_i,
  input  [7:0] k_i,
  input  [7:0] l_i,
  input  [7:0] m_i,
  input  [7:0] o_i,
  input  [7:0] p_i,
  input  [7:0] q_i,
  output [7:0] data_o
);

  wire [7:0] mux8_8b_1_data_o, mux8_8b_2_data_o;

  mux8_8b mux8_8b_1 (
    .sel_i(sel_i[2:0]), .a_i(a_i), .b_i(b_i), .c_i(c_i), .d_i(d_i), .e_i(e_i), .f_i(f_i), .g_i(g_i),
    .h_i(h_i), .data_o(mux8_8b_1_data_o));
  mux8_8b mux8_8b_2 (
    .sel_i(sel_i[2:0]), .a_i(i_i), .b_i(j_i), .c_i(k_i), .d_i(l_i), .e_i(m_i), .f_i(o_i), .g_i(p_i),
    .h_i(q_i), .data_o(mux8_8b_2_data_o));
  Multiplexer #(.width(8)) multiplexer_1 (.in0(mux8_8b_1_data_o), .in1(mux8_8b_2_data_o), .out(data_o), .sel(sel_i[3]));

  // Notes on the sheet:
  //   Copyright (c) 2026 Guiyuan Zhu. All rights reserved.
endmodule

module sCPU_gpr (
  input  [1:0] rd_addr0_i,
  input  [1:0] rd_addr1_i,
  input  [1:0] wr_addr_i,
  input  [7:0] wr_data_i,
  input  wr_en_i,
  input  rst_i,
  input  clk_i,
  output [7:0] rd_data0_o,
  output [7:0] rd_data1_o
);

  wire and_1_out, and_2_out, and_3_out, and_4_out;
  wire [3:0] decoder_2_4_1_data_o;
  wire [7:0] reg_8b_1_q_o, reg_8b_2_q_o, reg_8b_3_q_o, reg_8b_4_q_o;

  decoder_2_4 decoder_2_4_1 (.data_i(wr_addr_i), .data_o(decoder_2_4_1_data_o));
  and and_1 (and_1_out, decoder_2_4_1_data_o[0], wr_en_i);
  and and_2 (and_2_out, decoder_2_4_1_data_o[1], wr_en_i);
  and and_3 (and_3_out, decoder_2_4_1_data_o[2], wr_en_i);
  and and_4 (and_4_out, decoder_2_4_1_data_o[3], wr_en_i);
  reg_8b reg_8b_1 (.d_i(wr_data_i), .en_i(and_1_out), .rst_i(rst_i), .clk_i(clk_i), .q_o(reg_8b_1_q_o));
  // Probe on reg_8b_1_q_o
  reg_8b reg_8b_2 (.d_i(wr_data_i), .en_i(and_2_out), .rst_i(rst_i), .clk_i(clk_i), .q_o(reg_8b_2_q_o));
  // Probe on reg_8b_2_q_o
  reg_8b reg_8b_3 (.d_i(wr_data_i), .en_i(and_3_out), .rst_i(rst_i), .clk_i(clk_i), .q_o(reg_8b_3_q_o));
  // Probe on reg_8b_3_q_o
  reg_8b reg_8b_4 (.d_i(wr_data_i), .en_i(and_4_out), .rst_i(rst_i), .clk_i(clk_i), .q_o(reg_8b_4_q_o));
  // Probe on reg_8b_4_q_o
  mux4_8b mux4_8b_1 (
    .sel_i(rd_addr0_i), .a_i(reg_8b_1_q_o), .b_i(reg_8b_2_q_o), .c_i(reg_8b_3_q_o), .d_i(reg_8b_4_q_o),
    .e_o(rd_data0_o));
  mux4_8b mux4_8b_2 (
    .sel_i(rd_addr1_i), .a_i(reg_8b_1_q_o), .b_i(reg_8b_2_q_o), .c_i(reg_8b_3_q_o), .d_i(reg_8b_4_q_o),
    .e_o(rd_data1_o));

  // Notes on the sheet:
  //   Copyright (c) 2026 Guiyuan Zhu. All rights reserved.
endmodule

module sCPU_decoder (
  input  [7:0] inst_i,
  output is_add_o,
  output is_io_o,
  output is_li_o,
  output is_bner0_o,
  output [1:0] rd_o,
  output [1:0] rs1_o,
  output [1:0] rs2_o,
  output [7:0] imm_o,
  output [7:0] addr_o,
  output io_in_o,
  output io_out_o,
  output [2:0] dev_o
);

  wire [7:0] bit_extender_1_out;

  assign bit_extender_1_out = {{6{1'b0}}, inst_i[1:0]};  // Bit_Extender bit_extender_1
  Shifter shifter_1 (.in(bit_extender_1_out), .\dist ({inst_i[3:2], 1'b0}), .out(imm_o));
  assign addr_o = {{4{inst_i[5]}}, inst_i[5:2]};  // Bit_Extender bit_extender_2
  and and_1 (io_in_o, ~inst_i[3], is_io_o);  // AND_Gate
  and and_2 (io_out_o, inst_i[3], is_io_o);
  decoder_2_4 decoder_2_4_1 (.data_i(inst_i[7:6]), .data_o({is_bner0_o, is_li_o, is_io_o, is_add_o}));

  assign dev_o = inst_i[2:0];
  assign rd_o = inst_i[5:4];
  assign rs1_o = inst_i[3:2];
  assign rs2_o = inst_i[1:0];

  // Other names for the same wires on the sheet: dev[2:0] = inst_i[2:0]; offset[3:0] = inst_i[5:2];
  //   rs1[1:0] = inst_i[3:2]; io = inst_i[3]; is_io = is_io_o; imm[1:0] = inst_i[1:0]; rs2[1:0] = inst_i[1:0];
  //   rd[1:0] = inst_i[5:4]; op[1:0] = inst_i[7:6]

  // Notes on the sheet:
  //   Copyright (c) 2026 Guiyuan Zhu. All rights reserved.
endmodule

module sCPU (
  input  rst_i,
  input  clk_i,
  input  [7:0] inst_i,
  input  [7:0] idev0_i,
  input  [7:0] idev1_i,
  output [7:0] pc_o,
  output [7:0] odev0_o,
  output [7:0] odev1_o
);

  wire and_1_out, and_2_out, and_3_out, comparator_1_eq, dev0, dev1, gpr_wr_en, io_in, io_out, is_add,
       is_bner0, is_io, is_li, ner0;
  wire [1:0] multiplexer_3_out, multiplexer_4_out, rd, rs1, rs2;
  wire [2:0] dev;
  wire [7:0] addr, gpr_rd_val0, gpr_rd_val1, gpr_wr_val, imm, io_in_val, multiplexer_1_out,
       multiplexer_2_out, pc_nxt, sum_result;
  wire [7:2] decoder_3_8_1_data_o;

  Multiplexer #(.width(8)) multiplexer_1 (.in0(8'h1), .in1(addr), .out(multiplexer_1_out), .sel(and_1_out));
  and and_1 (and_1_out, is_bner0, ner0);
  sCPU_decoder scpu_decoder_1 (
    .inst_i(inst_i), .is_add_o(is_add), .is_io_o(is_io), .is_li_o(is_li), .is_bner0_o(is_bner0), .rd_o(rd),
    .rs1_o(rs1), .rs2_o(rs2), .imm_o(imm), .addr_o(addr), .io_in_o(io_in), .io_out_o(io_out), .dev_o(dev));
  rca_8b rca_8b_1 (.a_i(pc_o), .b_i(multiplexer_1_out), .sum_o(pc_nxt));  // open: cin_i, overflow_o, cout_o
  reg_8b reg_8b_1 (.d_i(pc_nxt), .en_i(1'b1), .rst_i(rst_i), .clk_i(clk_i), .q_o(pc_o));
  // Probe on pc_o
  Multiplexer #(.width(8)) multiplexer_2 (.in0(sum_result), .in1(imm), .out(multiplexer_2_out), .sel(is_li));
  Multiplexer #(.width(2)) multiplexer_3 (.in0(rs1), .in1(2'b00), .out(multiplexer_3_out), .sel(is_bner0));
  Multiplexer #(.width(2)) multiplexer_4 (.in0(rs2), .in1(rd), .out(multiplexer_4_out), .sel(is_io));
  // Probe on gpr_wr_val
  Multiplexer #(.width(8)) multiplexer_5 (.in0(multiplexer_2_out), .in1(io_in_val), .out(gpr_wr_val), .sel(io_in));
  not not_1 (ner0, comparator_1_eq);
  Comparator comparator_1 (.a(gpr_rd_val0), .b(gpr_rd_val1), .eq(comparator_1_eq));  // open: gt, lt
  // Probe on gpr_rd_val0
  sCPU_gpr scpu_gpr_1 (
    .rd_addr0_i(multiplexer_3_out), .rd_addr1_i(multiplexer_4_out), .wr_addr_i(rd), .wr_data_i(gpr_wr_val),
    .wr_en_i(gpr_wr_en), .rst_i(rst_i), .clk_i(clk_i), .rd_data0_o(gpr_rd_val0), .rd_data1_o(gpr_rd_val1));
  // Probe on gpr_rd_val1
  // Probe on sum_result
  rca_8b rca_8b_2 (.a_i(gpr_rd_val0), .b_i(gpr_rd_val1), .sum_o(sum_result));  // open: cin_i, overflow_o, cout_o
  or or_1 (gpr_wr_en, is_add, is_li, io_in);
  and and_2 (and_2_out, io_out, dev0);
  and and_3 (and_3_out, io_out, dev1);
  decoder_3_8 decoder_3_8_1 (.data_i(dev), .data_o({decoder_3_8_1_data_o, dev1, dev0}));
  // Probe on odev0_o
  reg_8b reg_8b_2 (.d_i(gpr_rd_val1), .en_i(and_2_out), .rst_i(rst_i), .clk_i(clk_i), .q_o(odev0_o));
  // Probe on odev1_o
  reg_8b reg_8b_3 (.d_i(gpr_rd_val1), .en_i(and_3_out), .rst_i(rst_i), .clk_i(clk_i), .q_o(odev1_o));
  mux8_8b mux8_8b_1 (
    .sel_i(dev), .a_i(idev0_i), .b_i(idev1_i), .data_o(io_in_val));  // open: c_i, d_i, e_i, f_i, g_i, h_i

  // Other names for the same wires on the sheet: pc[7:0] = pc_o

  // Notes on the sheet:
  //   Copyright (c) 2026 Guiyuan Zhu. All rights reserved.
endmodule

module sCPU_rom_sum_1_to_10 (
  input  [7:0] addr_i,
  output [7:0] inst_o
);

  mux16_8b mux16_8b_1 (
    .sel_i(addr_i[3:0]), .a_i(8'h86), .b_i(8'h92), .c_i(8'h1), .d_i(8'h90), .e_i(8'ha0), .f_i(8'hb1),
    .g_i(8'h17), .h_i(8'h29), .i_i(8'hf9), .j_i(8'h68), .k_i(8'h69), .l_i(8'hc3), .data_o(inst_o));  // open: m_i, o_i, p_i, q_i

  // Notes on the sheet:
  //   Copyright (c) 2026 Guiyuan Zhu. All rights reserved.
endmodule

module sCPU_top_sum_1_to_10 (
);

  wire clk_i, rst_i;
  wire [7:0] scpu_1_odev0_o, scpu_1_odev1_o, scpu_1_pc_o, scpu_rom_sum_1_to_10_1_inst_o;

  Button u_rst_i (.out(rst_i));
  Clock u_clk_i (.out(clk_i));
  sCPU_rom_sum_1_to_10 scpu_rom_sum_1_to_10_1 (.addr_i(scpu_1_pc_o), .inst_o(scpu_rom_sum_1_to_10_1_inst_o));
  sCPU scpu_1 (
    .rst_i(rst_i), .clk_i(clk_i), .inst_i(scpu_rom_sum_1_to_10_1_inst_o), .pc_o(scpu_1_pc_o),
    .odev0_o(scpu_1_odev0_o), .odev1_o(scpu_1_odev1_o));  // open: idev0_i, idev1_i
  // LedBar #(.inputtype("row")) ledbar_1: pin names not known; wires that end beside it: scpu_1_odev0_o
  segment_mux segment_mux_1 (.data_i(scpu_1_odev1_o[7:4]));  // open: dec_i
  segment_mux segment_mux_2 (.data_i(scpu_1_odev1_o[3:0]));  // open: dec_i

  // Notes on the sheet:
  //   Copyright (c) 2026 Guiyuan Zhu. All rights reserved.
endmodule

module sCPU_rom_sum_1_to_10_odd (
  input  [7:0] addr_i,
  output [7:0] inst_o
);

  mux16_8b mux16_8b_1 (
    .sel_i(addr_i[3:0]), .a_i(8'h86), .b_i(8'h91), .c_i(8'h1), .d_i(8'ha1), .e_i(8'hb2), .f_i(8'h17),
    .g_i(8'h29), .h_i(8'hf9), .i_i(8'h68), .j_i(8'h69), .k_i(8'hc3), .data_o(inst_o));  // open: l_i, m_i, o_i, p_i, q_i

  // Notes on the sheet:
  //   Copyright (c) 2026 Guiyuan Zhu. All rights reserved.
endmodule

module sCPU_top_sum_1_to_10_odd (
);

  wire clk_i, rst_i;
  wire [7:0] scpu_1_odev0_o, scpu_1_odev1_o, scpu_1_pc_o, scpu_rom_sum_1_to_10_1_inst_o;

  Button u_rst_i (.out(rst_i));
  Clock u_clk_i (.out(clk_i));
  sCPU_rom_sum_1_to_10 scpu_rom_sum_1_to_10_1 (.addr_i(scpu_1_pc_o), .inst_o(scpu_rom_sum_1_to_10_1_inst_o));
  sCPU scpu_1 (
    .rst_i(rst_i), .clk_i(clk_i), .inst_i(scpu_rom_sum_1_to_10_1_inst_o), .pc_o(scpu_1_pc_o),
    .odev0_o(scpu_1_odev0_o), .odev1_o(scpu_1_odev1_o));  // open: idev0_i, idev1_i
  // LedBar #(.inputtype("row")) ledbar_1: pin names not known; wires that end beside it: scpu_1_odev0_o
  segment_mux segment_mux_1 (.data_i(scpu_1_odev1_o[7:4]));  // open: dec_i
  segment_mux segment_mux_2 (.data_i(scpu_1_odev1_o[3:0]));  // open: dec_i

  // Notes on the sheet:
  //   Copyright (c) 2026 Guiyuan Zhu. All rights reserved.
endmodule

module sCPU_rom_sum_1_to_N (
  input  [7:0] addr_i,
  output [7:0] inst_o
);

  mux16_8b mux16_8b_1 (
    .sel_i(addr_i[3:0]), .a_i(8'h40), .b_i(8'h40), .c_i(8'h90), .d_i(8'ha0), .e_i(8'hb1), .f_i(8'h17),
    .g_i(8'h29), .h_i(8'hf9), .i_i(8'h68), .j_i(8'h80), .k_i(8'h91), .l_i(8'h71), .m_i(8'hcb), .o_i(8'hf9),
    .p_i(8'h69), .q_i(8'hc3), .data_o(inst_o));

  // Notes on the sheet:
  //   Copyright (c) 2026 Guiyuan Zhu. All rights reserved.
endmodule

module sCPU_top_sum_1_to_N (
);

  wire clk_i, rst_i;
  wire [7:0] button_8_out, dipswitch_1_sw8, scpu_1_odev0_o, scpu_1_odev1_o, scpu_1_pc_o,
       scpu_rom_sum_1_to_n_1_inst_o;

  Button u_rst_i (.out(rst_i));
  Clock u_clk_i (.out(clk_i));
  DipSwitch dipswitch_1 (
    .sw1(dipswitch_1_sw8[7]), .sw2(dipswitch_1_sw8[6]), .sw3(dipswitch_1_sw8[5]), .sw4(dipswitch_1_sw8[4]),
    .sw5(dipswitch_1_sw8[3]), .sw6(dipswitch_1_sw8[2]), .sw7(dipswitch_1_sw8[1]), .sw8(dipswitch_1_sw8[0]));
  Button button_1 (.out(button_8_out[7]));
  Button button_2 (.out(button_8_out[6]));
  sCPU_rom_sum_1_to_N scpu_rom_sum_1_to_n_1 (.addr_i(scpu_1_pc_o), .inst_o(scpu_rom_sum_1_to_n_1_inst_o));
  Button button_3 (.out(button_8_out[5]));
  Button button_4 (.out(button_8_out[3]));
  Button button_5 (.out(button_8_out[1]));
  Button button_6 (.out(button_8_out[4]));
  Button button_7 (.out(button_8_out[2]));
  Button button_8 (.out(button_8_out[0]));
  sCPU scpu_1 (
    .rst_i(rst_i), .clk_i(clk_i), .inst_i(scpu_rom_sum_1_to_n_1_inst_o), .idev0_i(dipswitch_1_sw8),
    .idev1_i(button_8_out), .pc_o(scpu_1_pc_o), .odev0_o(scpu_1_odev0_o), .odev1_o(scpu_1_odev1_o));
  // LedBar #(.inputtype("row")) ledbar_1: pin names not known; wires that end beside it: scpu_1_odev0_o
  segment_mux segment_mux_1 (.data_i(scpu_1_odev1_o[7:4]));  // open: dec_i
  segment_mux segment_mux_2 (.data_i(scpu_1_odev1_o[3:0]));  // open: dec_i

  // Notes on the sheet:
  //   Copyright (c) 2026 Guiyuan Zhu. All rights reserved.
endmodule

module sCPU_rom_1_to_N_step_v1 (
  input  [7:0] addr_i,
  output [7:0] inst_o
);

  mux16_8b mux16_8b_1 (
    .sel_i(addr_i[3:0]), .a_i(8'h90), .b_i(8'ha0), .c_i(8'hb1), .d_i(8'h1d), .e_i(8'h29), .f_i(8'h58),
    .g_i(8'h69), .h_i(8'h41), .i_i({8{1'b1}}), .j_i(8'h40), .k_i(8'he1), .l_i(8'h80), .m_i(8'hc3),
    .data_o(inst_o));  // open: o_i, p_i, q_i

  // Notes on the sheet:
  //   Copyright (c) 2026 Guiyuan Zhu. All rights reserved.
endmodule

module sCPU_top_1_to_N_step_v1 (
);

  wire clk_i, rst_i;
  wire [7:0] button_9_out, dipswitch_1_sw8, scpu_1_odev0_o, scpu_1_odev1_o, scpu_1_pc_o,
       scpu_rom_1_to_n_step_v1_1_inst_o;

  Button button_1 (.out(rst_i));
  Clock clock_1 (.out(clk_i));
  DipSwitch dipswitch_1 (
    .sw1(dipswitch_1_sw8[7]), .sw2(dipswitch_1_sw8[6]), .sw3(dipswitch_1_sw8[5]), .sw4(dipswitch_1_sw8[4]),
    .sw5(dipswitch_1_sw8[3]), .sw6(dipswitch_1_sw8[2]), .sw7(dipswitch_1_sw8[1]), .sw8(dipswitch_1_sw8[0]));
  Button button_2 (.out(button_9_out[7]));
  Button button_3 (.out(button_9_out[6]));
  sCPU_rom_1_to_N_step_v1 scpu_rom_1_to_n_step_v1_1 (.addr_i(scpu_1_pc_o), .inst_o(scpu_rom_1_to_n_step_v1_1_inst_o));
  Button button_4 (.out(button_9_out[5]));
  Button button_5 (.out(button_9_out[3]));
  Button button_6 (.out(button_9_out[1]));
  Button button_7 (.out(button_9_out[4]));
  Button button_8 (.out(button_9_out[2]));
  Button button_9 (.out(button_9_out[0]));
  sCPU scpu_1 (
    .rst_i(rst_i), .clk_i(clk_i), .inst_i(scpu_rom_1_to_n_step_v1_1_inst_o), .idev0_i(dipswitch_1_sw8),
    .idev1_i(button_9_out), .pc_o(scpu_1_pc_o), .odev0_o(scpu_1_odev0_o), .odev1_o(scpu_1_odev1_o));
  // LedBar #(.inputtype("row")) ledbar_1: pin names not known; wires that end beside it: scpu_1_odev0_o
  segment_mux segment_mux_1 (.data_i(scpu_1_odev1_o[7:4]));  // open: dec_i
  segment_mux segment_mux_2 (.data_i(scpu_1_odev1_o[3:0]));  // open: dec_i

  // Notes on the sheet:
  //   Copyright (c) 2026 Guiyuan Zhu. All rights reserved.
endmodule

module sCPU_rom_1_to_N_step_v2 (
  input  [7:0] addr_i,
  output [7:0] inst_o
);

  wire [7:0] mux16_8b_1_data_o, mux16_8b_2_data_o;

  mux16_8b mux16_8b_1 (
    .sel_i(addr_i[3:0]), .a_i(8'h90), .b_i(8'ha0), .c_i(8'hb1), .d_i(8'h1d), .e_i(8'h29), .f_i(8'h58),
    .g_i(8'h69), .h_i(8'h40), .i_i(8'hd1), .j_i(8'h80), .k_i(8'hc3), .l_i(8'he3), .m_i(8'h41),
    .o_i({8{1'b1}}), .p_i(8'h41), .q_i(8'hf3), .data_o(mux16_8b_1_data_o));
  mux16_8b mux16_8b_2 (
    .sel_i(addr_i[3:0]), .a_i(8'h80), .b_i(8'hf7), .data_o(mux16_8b_2_data_o));  // open: c_i, d_i, e_i, f_i, g_i, h_i, i_i, j_i, k_i, l_i, m_i, o_i, p_i, q_i
  Multiplexer #(.width(8)) multiplexer_1 (
    .in0(mux16_8b_1_data_o), .in1(mux16_8b_2_data_o), .out(inst_o), .sel(addr_i[4]));

  // Notes on the sheet:
  //   Copyright (c) 2026 Guiyuan Zhu. All rights reserved.
endmodule

module sCPU_top_1_to_N_step_v2 (
);

  wire clk_i, rst_i;
  wire [7:0] button_9_out, dipswitch_1_sw8, scpu_1_odev0_o, scpu_1_odev1_o, scpu_1_pc_o,
       scpu_rom_1_to_n_step_v2_1_inst_o;

  Button button_1 (.out(rst_i));
  Clock clock_1 (.out(clk_i));
  DipSwitch dipswitch_1 (
    .sw1(dipswitch_1_sw8[7]), .sw2(dipswitch_1_sw8[6]), .sw3(dipswitch_1_sw8[5]), .sw4(dipswitch_1_sw8[4]),
    .sw5(dipswitch_1_sw8[3]), .sw6(dipswitch_1_sw8[2]), .sw7(dipswitch_1_sw8[1]), .sw8(dipswitch_1_sw8[0]));
  Button button_2 (.out(button_9_out[7]));
  Button button_3 (.out(button_9_out[6]));
  sCPU_rom_1_to_N_step_v2 scpu_rom_1_to_n_step_v2_1 (.addr_i(scpu_1_pc_o), .inst_o(scpu_rom_1_to_n_step_v2_1_inst_o));
  Button button_4 (.out(button_9_out[5]));
  Button button_5 (.out(button_9_out[3]));
  Button button_6 (.out(button_9_out[1]));
  Button button_7 (.out(button_9_out[4]));
  Button button_8 (.out(button_9_out[2]));
  Button button_9 (.out(button_9_out[0]));
  sCPU scpu_1 (
    .rst_i(rst_i), .clk_i(clk_i), .inst_i(scpu_rom_1_to_n_step_v2_1_inst_o), .idev0_i(dipswitch_1_sw8),
    .idev1_i(button_9_out), .pc_o(scpu_1_pc_o), .odev0_o(scpu_1_odev0_o), .odev1_o(scpu_1_odev1_o));
  // LedBar #(.inputtype("row")) ledbar_1: pin names not known; wires that end beside it: scpu_1_odev0_o
  segment_mux segment_mux_1 (.data_i(scpu_1_odev1_o[7:4]));  // open: dec_i
  segment_mux segment_mux_2 (.data_i(scpu_1_odev1_o[3:0]));  // open: dec_i

  // Notes on the sheet:
  //   Copyright (c) 2026 Guiyuan Zhu. All rights reserved.
endmodule
